// Logisim project 实验1-CS1906-U201915115-郑舟.circ as structural Verilog: 5 circuits, main circuit 一位二进制半加器
module \一位二进制半加器  (
  input  A,
  input  B,
  output S,
  output C
);

  xor xor_1 (S, A, B);
  and and_1 (C, A, B);
endmodule

module \一位二进制全加器  (
  input  A,
  input  B,
  input  C,
  output S,
  output C_2
);

  wire and_1_out, and_2_out, xor_1_out;

  xor xor_1 (xor_1_out, A, B);
  and and_1 (and_1_out, xor_1_out, C);
  and and_2 (and_2_out, A, B);
  xor xor_2 (S, xor_1_out, C);
  or or_1 (C_2, and_1_out, and_2_out);
endmodule

module \串行进位并行加法器  (
  input  A3,
  input  B3,
  input  A2,
  input  B2,
  input  A1,
  input  B1,
  input  A0,
  input  B0,
  input  C0,
  output C4,
  output S3,
  output S2,
  output S1,
  output S0
);

  wire and_1_out, and_2_out, and_3_out, and_4_out, and_5_out, and_6_out, and_7_out, and_8_out, or_2_out,
       or_3_out, or_4_out, xor_1_out, xor_2_out, xor_3_out, xor_4_out;

  xor xor_1 (xor_1_out, A3, B3);
  xor xor_2 (xor_2_out, A2, B2);
  xor xor_3 (xor_3_out, A1, B1);
  xor xor_4 (xor_4_out, A0, B0);
  and and_1 (and_1_out, B3, A3);
  and and_2 (and_2_out, or_2_out, xor_1_out);
  and and_3 (and_3_out, B2, A2);
  and and_4 (and_4_out, or_3_out, xor_2_out);
  and and_5 (and_5_out, B1, A1);
  and and_6 (and_6_out, or_4_out, xor_3_out);
  and and_7 (and_7_out, B0, A0);
  and and_8 (and_8_out, C0, xor_4_out);
  or or_1 (C4, and_1_out, and_2_out);
  xor xor_5 (S3, xor_1_out, or_2_out);
  or or_2 (or_2_out, and_3_out, and_4_out);
  xor xor_6 (S2, xor_2_out, or_3_out);
  or or_3 (or_3_out, and_5_out, and_6_out);
  xor xor_7 (S1, xor_3_out, or_4_out);
  or or_4 (or_4_out, and_7_out, and_8_out);
  xor xor_8 (S0, xor_4_out, C0);
endmodule

module \先行进位并行加法器  (
  input  A3,
  input  B3,
  input  A2,
  input  B2,
  input  A1,
  input  B1,
  input  A0,
  input  B0,
  input  C0,
  output C4,
  output S3,
  output S2,
  output S1,
  output S0
);

  wire and_1_out, and_2_out, and_3_out, and_4_out, and_5_out, and_6_out, and_7_out, and_8_out, and_9_out,
       and_10_out, and_11_out, and_12_out, and_13_out, and_14_out, or_2_out, or_3_out, or_4_out, xor_1_out,
       xor_2_out, xor_3_out, xor_4_out;

  and and_1 (and_1_out, A3, B3);
  xor xor_1 (xor_1_out, A3, B3);
  and and_2 (and_2_out, A2, B2);
  xor xor_2 (xor_2_out, A2, B2);
  and and_3 (and_3_out, A1, B1);
  xor xor_3 (xor_3_out, A1, B1);
  and and_4 (and_4_out, A0, B0);
  xor xor_4 (xor_4_out, A0, B0);
  and and_5 (and_5_out, and_4_out, xor_3_out, xor_2_out);
  and and_6 (and_6_out, and_3_out, xor_2_out);
  and and_7 (and_7_out, xor_4_out, C0, xor_3_out);
  and and_8 (and_8_out, and_4_out, xor_3_out);
  and and_9 (and_9_out, xor_4_out, C0, xor_3_out, xor_2_out, xor_1_out);
  and and_10 (and_10_out, and_4_out, xor_3_out, xor_2_out, xor_1_out);
  and and_11 (and_11_out, and_3_out, xor_2_out, xor_1_out);
  and and_12 (and_12_out, and_2_out, xor_1_out);
  and and_13 (and_13_out, C0, xor_4_out, xor_3_out, xor_2_out);
  and and_14 (and_14_out, xor_4_out, C0);
  or or_1 (C4, and_1_out, and_9_out, and_10_out, and_11_out, and_12_out);
  or or_2 (or_2_out, and_2_out, and_13_out, and_5_out, and_6_out);
  or or_3 (or_3_out, and_3_out, and_7_out, and_8_out);
  or or_4 (or_4_out, and_4_out, and_14_out);
  xor xor_5 (S3, xor_1_out, or_2_out);
  xor xor_6 (S2, xor_2_out, or_3_out);
  xor xor_7 (S1, xor_3_out, or_4_out);
  xor xor_8 (S0, xor_4_out, C0);
endmodule

module \先行进位并行加法器测试电路  (
  input  in_1,
  input  in_2,
  input  in_3,
  input  in_4,
  input  in_5,
  input  in_6,
  input  in_7,
  input  in_8,
  input  in_9,
  output out_10,
  output out_11,
  output out_12,
  output out_13,
  output out_14
);

  \先行进位并行加法器  \u_先行进位并行加法器_1  (
    .A3(in_2), .B3(in_6), .A2(in_3), .B2(in_7), .A1(in_4), .B1(in_8), .A0(in_5), .B0(in_9), .C0(in_1),
    .C4(out_14), .S3(out_10), .S2(out_11), .S1(out_12), .S0(out_13));
endmodule
