// Logisim project 实验2-CS1906-U201915115-郑舟.circ as structural Verilog: 10 circuits, main circuit 四位二进制可逆计数器
module \先行进位并行加法器  (
  input  A3,
  input  B3,
  input  A2,
  input  B2,
  input  A1,
  input  B1,
  input  A0,
  input  B0,
  input  C0,
  output C4,
  output S3,
  output S2,
  output S1,
  output S0
);

  wire and_1_out, and_2_out, and_3_out, and_4_out, and_5_out, and_6_out, and_7_out, and_8_out, and_9_out,
       and_10_out, and_11_out, and_12_out, and_13_out, and_14_out, or_2_out, or_3_out, or_4_out, xor_1_out,
       xor_2_out, xor_3_out, xor_4_out;

  and and_1 (and_1_out, A3, B3);
  xor xor_1 (xor_1_out, A3, B3);
  and and_2 (and_2_out, A2, B2);
  xor xor_2 (xor_2_out, A2, B2);
  and and_3 (and_3_out, A1, B1);
  xor xor_3 (xor_3_out, A1, B1);
  and and_4 (and_4_out, A0, B0);
  xor xor_4 (xor_4_out, A0, B0);
  and and_5 (and_5_out, and_4_out, xor_3_out, xor_2_out);
  and and_6 (and_6_out, and_3_out, xor_2_out);
  and and_7 (and_7_out, xor_4_out, C0, xor_3_out);
  and and_8 (and_8_out, and_4_out, xor_3_out);
  and and_9 (and_9_out, xor_4_out, C0, xor_3_out, xor_2_out, xor_1_out);
  and and_10 (and_10_out, and_4_out, xor_3_out, xor_2_out, xor_1_out);
  and and_11 (and_11_out, and_3_out, xor_2_out, xor_1_out);
  and and_12 (and_12_out, and_2_out, xor_1_out);
  and and_13 (and_13_out, C0, xor_4_out, xor_3_out, xor_2_out);
  and and_14 (and_14_out, xor_4_out, C0);
  or or_1 (C4, and_1_out, and_9_out, and_10_out, and_11_out, and_12_out);
  or or_2 (or_2_out, and_2_out, and_13_out, and_5_out, and_6_out);
  or or_3 (or_3_out, and_3_out, and_7_out, and_8_out);
  or or_4 (or_4_out, and_4_out, and_14_out);
  xor xor_5 (S3, xor_1_out, or_2_out);
  xor xor_6 (S2, xor_2_out, or_3_out);
  xor xor_7 (S1, xor_3_out, or_4_out);
  xor xor_8 (S0, xor_4_out, C0);
endmodule

module \四位二进制可逆计数器  (
  input  CLR,
  input  nLR,
  input  A,
  input  B,
  input  C,
  input  D,
  input  CPU,
  input  CPD,
  output QA,
  output QB,
  output QC,
  output QD
);

  wire and_1_out, and_2_out, and_3_out, and_4_out, and_5_out, and_6_out, and_7_out, and_8_out, and_9_out,
       and_10_out, and_11_out, and_12_out, and_13_out, and_14_out, d_ff_1_qn, d_ff_2_qn, d_ff_3_qn,
       d_ff_4_qn, not_1_out, not_2_out, not_3_out, not_4_out, not_5_out, or_1_out, or_2_out, or_3_out,
       or_4_out, or_5_out, or_6_out, or_7_out, or_8_out;

  not not_1 (not_1_out, nLR);
  not not_2 (not_2_out, A);
  not not_3 (not_3_out, B);
  not not_4 (not_4_out, C);
  not not_5 (not_5_out, D);
  and and_1 (and_1_out, not_2_out, not_1_out);
  and and_2 (and_2_out, not_3_out, not_1_out);
  and and_3 (and_3_out, not_4_out, not_1_out);
  and and_4 (and_4_out, not_5_out, not_1_out);
  and and_5 (and_5_out, not_1_out, A);
  and and_6 (and_6_out, not_1_out, B);
  and and_7 (and_7_out, not_1_out, C);
  and and_8 (and_8_out, not_1_out, D);
  or or_1 (or_1_out, CPU, CPD);
  and and_9 (and_9_out, CPU, QA);
  or or_2 (or_2_out, and_9_out, and_10_out);
  and and_10 (and_10_out, CPD, d_ff_1_qn);
  and and_11 (and_11_out, CPU, QA, QB);
  or or_3 (or_3_out, and_11_out, and_12_out);
  and and_12 (and_12_out, CPD, d_ff_1_qn, d_ff_2_qn);
  and and_13 (and_13_out, CPU, QC, QB, QA);
  or or_4 (or_4_out, and_13_out, and_14_out);
  and and_14 (and_14_out, CPD, d_ff_1_qn, d_ff_2_qn, d_ff_3_qn);
  or or_5 (or_5_out, CLR, and_1_out);
  or or_6 (or_6_out, CLR, and_2_out);
  or or_7 (or_7_out, CLR, and_3_out);
  or or_8 (or_8_out, CLR, and_4_out);
  D_Flip_Flop #(.trigger("falling")) d_ff_1 (
    .clk(or_1_out), .D(d_ff_1_qn), .Q(QA), .Qn(d_ff_1_qn), .preset(and_5_out), .reset(or_5_out));
  D_Flip_Flop #(.trigger("falling")) d_ff_2 (
    .clk(or_2_out), .D(d_ff_2_qn), .Q(QB), .Qn(d_ff_2_qn), .preset(and_6_out), .reset(or_6_out));
  D_Flip_Flop #(.trigger("falling")) d_ff_3 (
    .clk(or_3_out), .D(d_ff_3_qn), .Q(QC), .Qn(d_ff_3_qn), .preset(and_7_out), .reset(or_7_out));
  D_Flip_Flop #(.trigger("falling")) d_ff_4 (
    .clk(or_4_out), .D(d_ff_4_qn), .Q(QD), .Qn(d_ff_4_qn), .preset(and_8_out), .reset(or_8_out));
endmodule

module \四位二进制可逆计数器测试电路  (
  input  D,
  input  C,
  input  B,
  input  A,
  input  nLR,
  output QD,
  output QC,
  output QB,
  output QA
);

  wire CLR_out, CPD_out, CPU_out;

  Button CPU (.out(CPU_out));
  Button CLR (.out(CLR_out));
  Button CPD (.out(CPD_out));
  \四位二进制可逆计数器  \u_四位二进制可逆计数器_1  (
    .CLR(CLR_out), .nLR(nLR), .A(A), .B(B), .C(C), .D(D), .QA(QA), .QB(QB), .QC(QC), .QD(QD), .CPU(CPU_out),
    .CPD(CPD_out));
endmodule

module \二进制转8421BCD码电路  (
  input  A3,
  input  A2,
  input  A1,
  input  A1_2,
  output S7,
  output S6,
  output S5,
  output S4,
  output S3,
  output S2,
  output S1,
  output S0
);

  wire and_1_out, and_2_out, or_1_out;

  \先行进位并行加法器  \u_先行进位并行加法器_1  (
    .A3(A3), .B3(1'b0), .A2(A2), .B2(or_1_out), .A1(A1), .B1(or_1_out), .A0(A1_2), .B0(1'b0), .C0(1'b0),
    .C4(S4), .S3(S3), .S2(S2), .S1(S1), .S0(S0));
  and and_1 (and_1_out, A1, A3);
  or or_1 (or_1_out, and_1_out, and_2_out);
  and and_2 (and_2_out, A3, A2);

  assign S5 = 1'b0;
  assign S6 = 1'b0;
  assign S7 = 1'b0;
endmodule

module \二进制转8421BCD码测试电路  (
  input  A3,
  input  A2,
  input  A1,
  input  A0,
  output S7,
  output S6,
  output S5,
  output S4,
  output S3,
  output S2,
  output S1,
  output S0
);

  \二进制转8421BCD码电路  \u_二进制转8421bcd码电路_1  (
    .S7(S7), .S6(S6), .S5(S5), .S4(S4), .S2(S2), .S1(S1), .S0(S0), .S3(S3), .A3(A3), .A2(A2), .A1(A1),
    .A1_2(A0));
endmodule

module \显示电路  (
  input  A3,
  input  A2,
  input  A1,
  input  A0,
  output a,
  output b,
  output c,
  output d,
  output e,
  output f,
  output g
);

  wire and_1_out, and_2_out, and_3_out, and_4_out, and_5_out, and_6_out, and_7_out, and_8_out, and_9_out,
       and_10_out, and_11_out, and_12_out, and_13_out, and_14_out, and_15_out, and_16_out, and_17_out,
       and_18_out, and_19_out, and_20_out, and_21_out, and_22_out, and_23_out, and_24_out, and_25_out,
       and_26_out, and_27_out, and_28_out, and_29_out, not_1_out, not_2_out, not_3_out, not_4_out, not_5_out,
       not_6_out, not_7_out, not_8_out, not_9_out, not_10_out, not_11_out, not_12_out, not_13_out,
       not_14_out, not_15_out, not_16_out, not_17_out, not_18_out, not_19_out, not_20_out, not_21_out,
       not_22_out, not_23_out, not_24_out, not_25_out, not_26_out, not_27_out, not_28_out, not_29_out,
       not_30_out, not_31_out, not_32_out, not_33_out, not_34_out, not_35_out, not_36_out, not_37_out,
       not_38_out, not_39_out, not_40_out, not_41_out, not_42_out, not_43_out, not_44_out, not_45_out,
       not_46_out, not_47_out;

  not not_1 (not_1_out, A0);
  not not_2 (not_2_out, A2);
  not not_3 (not_3_out, A3);
  not not_4 (not_4_out, A3);
  not not_5 (not_5_out, A1);
  not not_6 (not_6_out, A1);
  not not_7 (not_7_out, A2);
  not not_8 (not_8_out, A3);
  not not_9 (not_9_out, A1);
  not not_10 (not_10_out, A2);
  not not_11 (not_11_out, A0);
  not not_12 (not_12_out, A1);
  not not_13 (not_13_out, A2);
  not not_14 (not_14_out, A3);
  not not_15 (not_15_out, A1);
  not not_16 (not_16_out, A2);
  not not_17 (not_17_out, A2);
  not not_18 (not_18_out, A3);
  not not_19 (not_19_out, A3);
  not not_20 (not_20_out, A0);
  not not_21 (not_21_out, A1);
  not not_22 (not_22_out, A3);
  not not_23 (not_23_out, A0);
  not not_24 (not_24_out, A2);
  not not_25 (not_25_out, A2);
  not not_26 (not_26_out, A3);
  not not_27 (not_27_out, A1);
  not not_28 (not_28_out, A0);
  not not_29 (not_29_out, A2);
  not not_30 (not_30_out, A0);
  not not_31 (not_31_out, A2);
  not not_32 (not_32_out, A3);
  not not_33 (not_33_out, A0);
  not not_34 (not_34_out, A1);
  not not_35 (not_35_out, A2);
  not not_36 (not_36_out, A0);
  not not_37 (not_37_out, A0);
  not not_38 (not_38_out, A1);
  not not_39 (not_39_out, A2);
  not not_40 (not_40_out, A1);
  not not_41 (not_41_out, A0);
  not not_42 (not_42_out, A1);
  not not_43 (not_43_out, A0);
  not not_44 (not_44_out, A2);
  not not_45 (not_45_out, A3);
  not not_46 (not_46_out, A1);
  not not_47 (not_47_out, A2);
  and and_1 (and_1_out, not_1_out, not_2_out, not_3_out);
  and and_2 (and_2_out, A0, A1, not_4_out);
  and and_3 (and_3_out, A0, not_5_out, A2);
  and and_4 (and_4_out, not_6_out, not_7_out, A3);
  and and_5 (and_5_out, A0, A1, not_8_out);
  and and_6 (and_6_out, not_9_out, not_10_out, A3);
  and and_7 (and_7_out, not_11_out, not_12_out);
  and and_8 (and_8_out, not_13_out, not_14_out);
  and and_9 (and_9_out, not_15_out, not_16_out, A3);
  and and_10 (and_10_out, A0, A1, not_17_out);
  and and_11 (and_11_out, A1, A2, not_18_out);
  and and_12 (and_12_out, A0, not_19_out);
  and and_13 (and_13_out, not_20_out, not_21_out, not_22_out);
  and and_14 (and_14_out, not_23_out, A1);
  and and_15 (and_15_out, A1, not_24_out, A3);
  and and_16 (and_16_out, A1, not_25_out, not_26_out);
  and and_17 (and_17_out, A0, not_27_out, A2);
  and and_18 (and_18_out, not_28_out, not_29_out, A3);
  and and_19 (and_19_out, not_30_out, not_31_out, not_32_out);
  and and_20 (and_20_out, not_33_out, not_34_out, not_35_out);
  and and_21 (and_21_out, not_36_out, A1);
  and and_22 (and_22_out, not_37_out, A1, A2);
  and and_23 (and_23_out, A0, not_38_out, A2);
  and and_24 (and_24_out, not_39_out, not_40_out, A3);
  and and_25 (and_25_out, not_41_out, not_42_out);
  and and_26 (and_26_out, not_43_out, A1);
  and and_27 (and_27_out, A1, not_44_out, not_45_out);
  and and_28 (and_28_out, not_46_out, A2);
  and and_29 (and_29_out, not_47_out, A3);
  or or_1 (a, and_1_out, and_2_out, and_3_out, and_4_out);
  or or_2 (b, and_5_out, and_6_out, and_7_out, and_8_out);
  or or_3 (c, and_9_out, and_10_out, and_11_out, and_12_out, and_13_out);
  or or_4 (d, and_14_out, and_15_out, and_16_out, and_17_out, and_18_out, and_19_out);
  or or_5 (e, and_20_out, and_21_out);
  or or_6 (f, and_22_out, and_23_out, and_24_out, and_25_out);
  or or_7 (g, and_26_out, and_27_out, and_28_out, and_29_out);
endmodule

module \显示电路测试电路  (
  input  A3,
  input  A2,
  input  A1,
  input  A0
);

  wire \显示电路_1_a , \显示电路_1_b , \显示电路_1_c , \显示电路_1_d , \显示电路_1_e , \显示电路_1_f , \显示电路_1_g ;

  _7_Segment_Display u_7_segment_display_1 (
    .g(\显示电路_1_g ), .f(\显示电路_1_f ), .a(\显示电路_1_a ), .b(\显示电路_1_b ), .e(\显示电路_1_e ), .d(\显示电路_1_d ),
    .c(\显示电路_1_c ), .dp(1'b0));
  \显示电路  \u_显示电路_1  (
    .a(\显示电路_1_a ), .b(\显示电路_1_b ), .c(\显示电路_1_c ), .d(\显示电路_1_d ), .e(\显示电路_1_e ), .f(\显示电路_1_f ),
    .g(\显示电路_1_g ), .A3(A3), .A2(A2), .A1(A1), .A0(A0));
endmodule

module \报警电路  (
  input  CPU,
  input  CLR,
  input  CPD,
  input  D,
  input  C,
  input  B,
  input  A,
  input  nLR,
  output QD,
  output QC,
  output QB,
  output QA,
  output \报警 
);

  wire and_1_out, and_2_out, and_4_out, not_1_out, or_1_out;

  not not_1 (not_1_out, and_4_out);
  or or_1 (or_1_out, QA, QB, QC, QD);
  and and_1 (and_1_out, CPU, not_1_out);
  and and_2 (and_2_out, or_1_out, CPD);
  \四位二进制可逆计数器  \u_四位二进制可逆计数器_1  (
    .CLR(CLR), .nLR(nLR), .A(A), .B(B), .C(C), .D(D), .QA(QA), .QB(QB), .QC(QC), .QD(QD), .CPU(and_1_out),
    .CPD(and_2_out));
  and and_3 (\报警 , CPU, and_4_out);
  and and_4 (and_4_out, QA, QB, QC, QD);
endmodule

module \小型实验室门禁系统电路的封装  (
  input  CPU,
  input  CLR,
  input  CPD,
  output a,
  output b,
  output c,
  output d,
  output e,
  output f,
  output g,
  output a_2,
  output b_2,
  output c_2,
  output d_2,
  output e_2,
  output f_2,
  output g_2,
  output \报警 
);

  wire \二进制转8421bcd码电路_1_s0 , \二进制转8421bcd码电路_1_s1 , \二进制转8421bcd码电路_1_s2 , \二进制转8421bcd码电路_1_s3 ,
       \二进制转8421bcd码电路_1_s4 , \二进制转8421bcd码电路_1_s5 , \二进制转8421bcd码电路_1_s6 , \二进制转8421bcd码电路_1_s7 ,
       \报警电路_1_qa , \报警电路_1_qb , \报警电路_1_qc , \报警电路_1_qd ;

  \显示电路  \u_显示电路_1  (
    .a(a), .b(b), .c(c), .d(d), .e(e), .f(f), .g(g), .A3(\二进制转8421bcd码电路_1_s7 ), .A2(\二进制转8421bcd码电路_1_s6 ),
    .A1(\二进制转8421bcd码电路_1_s5 ), .A0(\二进制转8421bcd码电路_1_s4 ));
  \二进制转8421BCD码电路  \u_二进制转8421bcd码电路_1  (
    .S7(\二进制转8421bcd码电路_1_s7 ), .S6(\二进制转8421bcd码电路_1_s6 ), .S5(\二进制转8421bcd码电路_1_s5 ),
    .S4(\二进制转8421bcd码电路_1_s4 ), .S2(\二进制转8421bcd码电路_1_s2 ), .S1(\二进制转8421bcd码电路_1_s1 ),
    .S0(\二进制转8421bcd码电路_1_s0 ), .S3(\二进制转8421bcd码电路_1_s3 ), .A3(\报警电路_1_qd ), .A2(\报警电路_1_qc ),
    .A1(\报警电路_1_qb ), .A1_2(\报警电路_1_qa ));
  \报警电路  \u_报警电路_1  (
    .CPU(CPU), .CLR(CLR), .CPD(CPD), .\报警 (\报警 ), .QD(\报警电路_1_qd ), .QC(\报警电路_1_qc ), .QB(\报警电路_1_qb ),
    .QA(\报警电路_1_qa ), .D(1'b0), .C(1'b0), .B(1'b0), .A(1'b0), .nLR(1'b1));
  \显示电路  \u_显示电路_2  (
    .a(a_2), .b(b_2), .c(c_2), .d(d_2), .e(e_2), .f(f_2), .g(g_2), .A3(\二进制转8421bcd码电路_1_s3 ),
    .A2(\二进制转8421bcd码电路_1_s2 ), .A1(\二进制转8421bcd码电路_1_s1 ), .A0(\二进制转8421bcd码电路_1_s0 ));
endmodule

module \小型实验室门禁系统电路测试电路  (
);

  wire CLR_out, CPD_out, CPU_out, \小型实验室门禁系统电路的封装_1_a , \小型实验室门禁系统电路的封装_1_a_2 , \小型实验室门禁系统电路的封装_1_b ,
       \小型实验室门禁系统电路的封装_1_b_2 , \小型实验室门禁系统电路的封装_1_c , \小型实验室门禁系统电路的封装_1_c_2 , \小型实验室门禁系统电路的封装_1_d ,
       \小型实验室门禁系统电路的封装_1_d_2 , \小型实验室门禁系统电路的封装_1_e , \小型实验室门禁系统电路的封装_1_e_2 , \小型实验室门禁系统电路的封装_1_f ,
       \小型实验室门禁系统电路的封装_1_f_2 , \小型实验室门禁系统电路的封装_1_g , \小型实验室门禁系统电路的封装_1_g_2 , \小型实验室门禁系统电路的封装_1_报警 ;

  Button CPU (.out(CPU_out));
  Button CLR (.out(CLR_out));
  Button CPD (.out(CPD_out));
  _7_Segment_Display u_7_segment_display_1 (
    .g(\小型实验室门禁系统电路的封装_1_g ), .f(\小型实验室门禁系统电路的封装_1_f ), .a(\小型实验室门禁系统电路的封装_1_a ), .b(\小型实验室门禁系统电路的封装_1_b ),
    .e(\小型实验室门禁系统电路的封装_1_e ), .d(\小型实验室门禁系统电路的封装_1_d ), .c(\小型实验室门禁系统电路的封装_1_c ), .dp(1'b0));
  _7_Segment_Display u_7_segment_display_2 (
    .g(\小型实验室门禁系统电路的封装_1_g_2 ), .f(\小型实验室门禁系统电路的封装_1_f_2 ), .a(\小型实验室门禁系统电路的封装_1_a_2 ),
    .b(\小型实验室门禁系统电路的封装_1_b_2 ), .e(\小型实验室门禁系统电路的封装_1_e_2 ), .d(\小型实验室门禁系统电路的封装_1_d_2 ),
    .c(\小型实验室门禁系统电路的封装_1_c_2 ), .dp(1'b0));
  LED led_1 (.in(\小型实验室门禁系统电路的封装_1_报警 ));
  \小型实验室门禁系统电路的封装  \u_小型实验室门禁系统电路的封装_1  (
    .CPU(CPU_out), .CLR(CLR_out), .CPD(CPD_out), .\报警 (\小型实验室门禁系统电路的封装_1_报警 ), .a(\小型实验室门禁系统电路的封装_1_a ),
    .b(\小型实验室门禁系统电路的封装_1_b ), .c(\小型实验室门禁系统电路的封装_1_c ), .d(\小型实验室门禁系统电路的封装_1_d ), .e(\小型实验室门禁系统电路的封装_1_e ),
    .f(\小型实验室门禁系统电路的封装_1_f ), .g(\小型实验室门禁系统电路的封装_1_g ), .a_2(\小型实验室门禁系统电路的封装_1_a_2 ),
    .b_2(\小型实验室门禁系统电路的封装_1_b_2 ), .c_2(\小型实验室门禁系统电路的封装_1_c_2 ), .d_2(\小型实验室门禁系统电路的封装_1_d_2 ),
    .e_2(\小型实验室门禁系统电路的封装_1_e_2 ), .f_2(\小型实验室门禁系统电路的封装_1_f_2 ), .g_2(\小型实验室门禁系统电路的封装_1_g_2 ));
endmodule
