// Logisim project 实验4-CS1906-U201915115-郑舟.circ as structural Verilog: 4 circuits, main circuit 四位除法器
module \四位除法器  (
  input  [3:0] d_3_0,
  input  [3:0] n2_3_0,
  output [3:0] rem_3_0,
  output [3:0] quot_3_0
);

  wire comparator_1_gt, comparator_2_gt, comparator_3_gt, comparator_4_gt;
  wire [3:0] multiplexer_1_out, multiplexer_2_out, multiplexer_3_out, multiplexer_4_out, multiplexer_5_out,
       multiplexer_6_out, or_1_out, or_2_out, or_3_out, or_4_out, subtractor_1_out, subtractor_2_out,
       subtractor_3_out, subtractor_4_out;
  wire [7:0] bit_extender_1_out, shifter_1_out, shifter_2_out, shifter_3_out, shifter_4_out;

  assign bit_extender_1_out = {{4{1'b0}}, n2_3_0};  // Bit_Extender bit_extender_1
  Shifter shifter_1 (.in(bit_extender_1_out), .\dist (3'b001), .out(shifter_1_out));
  Comparator #(.width(4), .mode("unsigned")) comparator_1 (
    .a(d_3_0), .b(shifter_1_out[7:4]), .gt(comparator_1_gt));  // open: eq, lt
  Subtractor #(.width(4)) subtractor_1 (
    .a(shifter_1_out[7:4]), .b(d_3_0), .out(subtractor_1_out), .bin(1'b0));  // open: bout
  Multiplexer #(.width(4), .enable("false")) multiplexer_1 (
    .in0(subtractor_1_out), .in1(shifter_1_out[7:4]), .out(multiplexer_1_out), .sel(comparator_1_gt));
  assign or_1_out = shifter_1_out[3:0] | 4'b0001;  // OR_Gate or_1, 4 bits wide
  Multiplexer #(.width(4), .enable("false")) multiplexer_2 (
    .in0(or_1_out), .in1(shifter_1_out[3:0]), .out(multiplexer_2_out), .sel(comparator_1_gt));
  Shifter shifter_2 (.in({multiplexer_1_out, multiplexer_2_out}), .\dist (3'b001), .out(shifter_2_out));
  Comparator #(.width(4), .mode("unsigned")) comparator_2 (
    .a(d_3_0), .b(shifter_2_out[7:4]), .gt(comparator_2_gt));  // open: eq, lt
  assign or_2_out = shifter_2_out[3:0] | 4'b0001;  // OR_Gate or_2, 4 bits wide
  Subtractor #(.width(4)) subtractor_2 (
    .a(shifter_2_out[7:4]), .b(d_3_0), .out(subtractor_2_out), .bin(1'b0));  // open: bout
  Multiplexer #(.width(4), .enable("false")) multiplexer_3 (
    .in0(subtractor_2_out), .in1(shifter_2_out[7:4]), .out(multiplexer_3_out), .sel(comparator_2_gt));
  Multiplexer #(.width(4), .enable("false")) multiplexer_4 (
    .in0(or_2_out), .in1(shifter_2_out[3:0]), .out(multiplexer_4_out), .sel(comparator_2_gt));
  Shifter shifter_3 (.in({multiplexer_3_out, multiplexer_4_out}), .\dist (3'b001), .out(shifter_3_out));
  Comparator #(.width(4), .mode("unsigned")) comparator_3 (
    .a(d_3_0), .b(shifter_3_out[7:4]), .gt(comparator_3_gt));  // open: eq, lt
  Subtractor #(.width(4)) subtractor_3 (
    .a(shifter_3_out[7:4]), .b(d_3_0), .out(subtractor_3_out), .bin(1'b0));  // open: bout
  assign or_3_out = shifter_3_out[3:0] | 4'b0001;  // OR_Gate or_3, 4 bits wide
  Multiplexer #(.width(4), .enable("false")) multiplexer_5 (
    .in0(subtractor_3_out), .in1(shifter_3_out[7:4]), .out(multiplexer_5_out), .sel(comparator_3_gt));
  Multiplexer #(.width(4), .enable("false")) multiplexer_6 (
    .in0(or_3_out), .in1(shifter_3_out[3:0]), .out(multiplexer_6_out), .sel(comparator_3_gt));
  Shifter shifter_4 (.in({multiplexer_5_out, multiplexer_6_out}), .\dist (3'b001), .out(shifter_4_out));
  Comparator #(.width(4), .mode("unsigned")) comparator_4 (
    .a(d_3_0), .b(shifter_4_out[7:4]), .gt(comparator_4_gt));  // open: eq, lt
  Subtractor #(.width(4)) subtractor_4 (
    .a(shifter_4_out[7:4]), .b(d_3_0), .out(subtractor_4_out), .bin(1'b0));  // open: bout
  assign or_4_out = shifter_4_out[3:0] | 4'b0001;  // OR_Gate or_4, 4 bits wide
  Multiplexer #(.width(4), .enable("false")) multiplexer_7 (
    .in0(subtractor_4_out), .in1(shifter_4_out[7:4]), .out(rem_3_0), .sel(comparator_4_gt));
  Multiplexer #(.width(4), .enable("false")) multiplexer_8 (
    .in0(or_4_out), .in1(shifter_4_out[3:0]), .out(quot_3_0), .sel(comparator_4_gt));
endmodule

module \四位除法器测试电路  (
  input  [3:0] \被除数 ,
  input  [3:0] \除数 ,
  output [3:0] \商 ,
  output [3:0] \余数 
);

  \四位除法器  \u_四位除法器_1  (.d_3_0(\除数 ), .n2_3_0(\被除数 ), .rem_3_0(\余数 ), .quot_3_0(\商 ));
endmodule

module \_32位除法器  (
  input  [31:0] d_31_0,
  input  [31:0] n_31_0,
  output [31:0] rem_31_0,
  output [31:0] quot_31_0
);

  wire comparator_1_gt, comparator_2_gt, comparator_3_gt, comparator_4_gt, comparator_5_gt, comparator_6_gt,
       comparator_7_gt, comparator_8_gt, comparator_9_gt, comparator_10_gt, comparator_11_gt,
       comparator_12_gt, comparator_13_gt, comparator_14_gt, comparator_15_gt, comparator_16_gt,
       comparator_17_gt, comparator_18_gt, comparator_19_gt, comparator_20_gt, comparator_21_gt,
       comparator_22_gt, comparator_23_gt, comparator_24_gt, comparator_25_gt, comparator_26_gt,
       comparator_27_gt, comparator_28_gt, comparator_29_gt, comparator_30_gt, comparator_31_gt,
       comparator_32_gt;
  wire [31:0] multiplexer_2_out_2, multiplexer_4_out, multiplexer_6_out, multiplexer_7_out,
       multiplexer_8_out, multiplexer_9_out, multiplexer_10_out, multiplexer_11_out, multiplexer_12_out,
       multiplexer_13_out, multiplexer_14_out, multiplexer_15_out, multiplexer_16_out, multiplexer_17_out,
       multiplexer_18_out, multiplexer_19_out, multiplexer_20_out, multiplexer_21_out, multiplexer_22_out,
       multiplexer_23_out, multiplexer_24_out, multiplexer_25_out, multiplexer_26_out, multiplexer_27_out,
       multiplexer_28_out, multiplexer_29_out, multiplexer_30_out, multiplexer_31_out, multiplexer_32_out,
       multiplexer_33_out, multiplexer_34_out, multiplexer_35_out, multiplexer_36_out, multiplexer_37_out,
       multiplexer_38_out, multiplexer_39_out, multiplexer_40_out, multiplexer_41_out, multiplexer_42_out,
       multiplexer_43_out, multiplexer_44_out, multiplexer_45_out, multiplexer_46_out, multiplexer_47_out,
       multiplexer_48_out, multiplexer_49_out, multiplexer_50_out, multiplexer_51_out, multiplexer_52_out,
       multiplexer_53_out, multiplexer_54_out, multiplexer_55_out, multiplexer_56_out, multiplexer_57_out,
       multiplexer_58_out, multiplexer_59_out, multiplexer_60_out, multiplexer_61_out, multiplexer_62_out,
       or_1_out, or_2_out, or_3_out, or_4_out, or_5_out, or_6_out, or_7_out, or_8_out, or_9_out, or_10_out,
       or_11_out, or_12_out, or_13_out, or_14_out, or_15_out, or_16_out, or_17_out, or_18_out, or_19_out,
       or_20_out, or_21_out, or_22_out, or_23_out, or_24_out, or_25_out, or_26_out, or_27_out, or_28_out,
       or_29_out, or_30_out, or_31_out, or_32_out, subtractor_1_out, subtractor_2_out, subtractor_3_out,
       subtractor_4_out, subtractor_5_out, subtractor_6_out, subtractor_7_out, subtractor_8_out,
       subtractor_9_out, subtractor_10_out, subtractor_11_out, subtractor_12_out, subtractor_13_out,
       subtractor_14_out, subtractor_15_out, subtractor_16_out, subtractor_17_out, subtractor_18_out,
       subtractor_19_out, subtractor_20_out, subtractor_21_out, subtractor_22_out, subtractor_23_out,
       subtractor_24_out, subtractor_25_out, subtractor_26_out, subtractor_27_out, subtractor_28_out,
       subtractor_29_out, subtractor_30_out, subtractor_31_out, subtractor_32_out;
  wire [31:1] multiplexer_2_out, multiplexer_4_out_2, multiplexer_6_out_2;
  wire [31:31] multiplexer_1_out, multiplexer_3_out, multiplexer_5_out;

  Comparator #(.width(32), .mode("unsigned")) comparator_1 (
    .a(d_31_0), .b({{31{1'b0}}, n_31_0[31]}), .gt(comparator_1_gt));  // open: eq, lt
  Subtractor #(.width(32)) subtractor_1 (
    .a({{31{1'b0}}, n_31_0[31]}), .b(d_31_0), .out(subtractor_1_out), .bin(1'b0));  // open: bout
  Multiplexer #(.width(32), .enable("false")) multiplexer_1 (
    .in0(subtractor_1_out), .in1({{31{1'b0}}, n_31_0[31]}),
    .out({multiplexer_1_out[31], multiplexer_2_out_2[31:1]}), .sel(comparator_1_gt));
  assign or_1_out = 32'h1 | {n_31_0[30:0], 1'b0};  // OR_Gate or_1, 32 bits wide
  Multiplexer #(.width(32), .enable("false")) multiplexer_2 (
    .in0(or_1_out), .in1({n_31_0[30:0], 1'b0}), .out({multiplexer_2_out_2[0], multiplexer_2_out}),
    .sel(comparator_1_gt));
  Comparator #(.width(32), .mode("unsigned")) comparator_2 (
    .a(d_31_0), .b({multiplexer_57_out[30:0], multiplexer_58_out[31]}), .gt(comparator_2_gt));  // open: eq, lt
  Subtractor #(.width(32)) subtractor_2 (
    .a({multiplexer_57_out[30:0], multiplexer_58_out[31]}), .b(d_31_0), .out(subtractor_2_out), .bin(1'b0));  // open: bout
  assign or_2_out = 32'h1 | {multiplexer_58_out[30:0], 1'b0};  // OR_Gate or_2, 32 bits wide
  Comparator #(.width(32), .mode("unsigned")) comparator_3 (
    .a(d_31_0), .b({multiplexer_59_out[30:0], multiplexer_60_out[31]}), .gt(comparator_3_gt));  // open: eq, lt
  Multiplexer #(.width(32), .enable("false")) multiplexer_3 (
    .in0(subtractor_2_out), .in1({multiplexer_57_out[30:0], multiplexer_58_out[31]}),
    .out({multiplexer_3_out[31], multiplexer_4_out[31:1]}), .sel(comparator_2_gt));
  Multiplexer #(.width(32), .enable("false")) multiplexer_4 (
    .in0(or_2_out), .in1({multiplexer_58_out[30:0], 1'b0}),
    .out({multiplexer_4_out[0], multiplexer_4_out_2}), .sel(comparator_2_gt));
  Subtractor #(.width(32)) subtractor_3 (
    .a({multiplexer_59_out[30:0], multiplexer_60_out[31]}), .b(d_31_0), .out(subtractor_3_out), .bin(1'b0));  // open: bout
  assign or_3_out = 32'h1 | {multiplexer_60_out[30:0], 1'b0};  // OR_Gate or_3, 32 bits wide
  Comparator #(.width(32), .mode("unsigned")) comparator_4 (
    .a(d_31_0), .b({multiplexer_61_out[30:0], multiplexer_62_out[31]}), .gt(comparator_4_gt));  // open: eq, lt
  Subtractor #(.width(32)) subtractor_4 (
    .a({multiplexer_61_out[30:0], multiplexer_62_out[31]}), .b(d_31_0), .out(subtractor_4_out), .bin(1'b0));  // open: bout
  Multiplexer #(.width(32), .enable("false")) multiplexer_5 (
    .in0(subtractor_3_out), .in1({multiplexer_59_out[30:0], multiplexer_60_out[31]}),
    .out({multiplexer_5_out[31], multiplexer_6_out[31:1]}), .sel(comparator_3_gt));
  Multiplexer #(.width(32), .enable("false")) multiplexer_6 (
    .in0(or_3_out), .in1({multiplexer_60_out[30:0], 1'b0}),
    .out({multiplexer_6_out[0], multiplexer_6_out_2}), .sel(comparator_3_gt));
  Multiplexer #(.width(32), .enable("false")) multiplexer_7 (
    .in0(subtractor_4_out), .in1({multiplexer_61_out[30:0], multiplexer_62_out[31]}),
    .out(multiplexer_7_out), .sel(comparator_4_gt));
  assign or_4_out = 32'h1 | {multiplexer_62_out[30:0], 1'b0};  // OR_Gate or_4, 32 bits wide
  Multiplexer #(.width(32), .enable("false")) multiplexer_8 (
    .in0(or_4_out), .in1({multiplexer_62_out[30:0], 1'b0}), .out(multiplexer_8_out), .sel(comparator_4_gt));
  Comparator #(.width(32), .mode("unsigned")) comparator_5 (
    .a(d_31_0), .b(multiplexer_2_out_2), .gt(comparator_5_gt));  // open: eq, lt
  Subtractor #(.width(32)) subtractor_5 (
    .a(multiplexer_2_out_2), .b(d_31_0), .out(subtractor_5_out), .bin(1'b0));  // open: bout
  Multiplexer #(.width(32), .enable("false")) multiplexer_9 (
    .in0(subtractor_5_out), .in1(multiplexer_2_out_2), .out(multiplexer_9_out), .sel(comparator_5_gt));
  assign or_5_out = 32'h1 | {multiplexer_2_out, 1'b0};  // OR_Gate or_5, 32 bits wide
  Multiplexer #(.width(32), .enable("false")) multiplexer_10 (
    .in0(or_5_out), .in1({multiplexer_2_out, 1'b0}), .out(multiplexer_10_out), .sel(comparator_5_gt));
  Comparator #(.width(32), .mode("unsigned")) comparator_6 (
    .a(d_31_0), .b(multiplexer_4_out), .gt(comparator_6_gt));  // open: eq, lt
  Subtractor #(.width(32)) subtractor_6 (
    .a(multiplexer_4_out), .b(d_31_0), .out(subtractor_6_out), .bin(1'b0));  // open: bout
  assign or_6_out = 32'h1 | {multiplexer_4_out_2, 1'b0};  // OR_Gate or_6, 32 bits wide
  Comparator #(.width(32), .mode("unsigned")) comparator_7 (
    .a(d_31_0), .b(multiplexer_6_out), .gt(comparator_7_gt));  // open: eq, lt
  Multiplexer #(.width(32), .enable("false")) multiplexer_11 (
    .in0(subtractor_6_out), .in1(multiplexer_4_out), .out(multiplexer_11_out), .sel(comparator_6_gt));
  Multiplexer #(.width(32), .enable("false")) multiplexer_12 (
    .in0(or_6_out), .in1({multiplexer_4_out_2, 1'b0}), .out(multiplexer_12_out), .sel(comparator_6_gt));
  Subtractor #(.width(32)) subtractor_7 (
    .a(multiplexer_6_out), .b(d_31_0), .out(subtractor_7_out), .bin(1'b0));  // open: bout
  assign or_7_out = 32'h1 | {multiplexer_6_out_2, 1'b0};  // OR_Gate or_7, 32 bits wide
  Comparator #(.width(32), .mode("unsigned")) comparator_8 (
    .a(d_31_0), .b({multiplexer_7_out[30:0], multiplexer_8_out[31]}), .gt(comparator_8_gt));  // open: eq, lt
  Subtractor #(.width(32)) subtractor_8 (
    .a({multiplexer_7_out[30:0], multiplexer_8_out[31]}), .b(d_31_0), .out(subtractor_8_out), .bin(1'b0));  // open: bout
  Multiplexer #(.width(32), .enable("false")) multiplexer_13 (
    .in0(subtractor_7_out), .in1(multiplexer_6_out), .out(multiplexer_13_out), .sel(comparator_7_gt));
  Multiplexer #(.width(32), .enable("false")) multiplexer_14 (
    .in0(or_7_out), .in1({multiplexer_6_out_2, 1'b0}), .out(multiplexer_14_out), .sel(comparator_7_gt));
  Multiplexer #(.width(32), .enable("false")) multiplexer_15 (
    .in0(subtractor_8_out), .in1({multiplexer_7_out[30:0], multiplexer_8_out[31]}), .out(multiplexer_15_out),
    .sel(comparator_8_gt));
  assign or_8_out = 32'h1 | {multiplexer_8_out[30:0], 1'b0};  // OR_Gate or_8, 32 bits wide
  Multiplexer #(.width(32), .enable("false")) multiplexer_16 (
    .in0(or_8_out), .in1({multiplexer_8_out[30:0], 1'b0}), .out(multiplexer_16_out), .sel(comparator_8_gt));
  Comparator #(.width(32), .mode("unsigned")) comparator_9 (
    .a(d_31_0), .b({multiplexer_9_out[30:0], multiplexer_10_out[31]}), .gt(comparator_9_gt));  // open: eq, lt
  Subtractor #(.width(32)) subtractor_9 (
    .a({multiplexer_9_out[30:0], multiplexer_10_out[31]}), .b(d_31_0), .out(subtractor_9_out), .bin(1'b0));  // open: bout
  assign or_9_out = 32'h1 | {multiplexer_10_out[30:0], 1'b0};  // OR_Gate or_9, 32 bits wide
  Comparator #(.width(32), .mode("unsigned")) comparator_10 (
    .a(d_31_0), .b({multiplexer_11_out[30:0], multiplexer_12_out[31]}), .gt(comparator_10_gt));  // open: eq, lt
  Subtractor #(.width(32)) subtractor_10 (
    .a({multiplexer_11_out[30:0], multiplexer_12_out[31]}), .b(d_31_0), .out(subtractor_10_out), .bin(1'b0));  // open: bout
  assign or_10_out = 32'h1 | {multiplexer_12_out[30:0], 1'b0};  // OR_Gate or_10, 32 bits wide
  Comparator #(.width(32), .mode("unsigned")) comparator_11 (
    .a(d_31_0), .b({multiplexer_13_out[30:0], multiplexer_14_out[31]}), .gt(comparator_11_gt));  // open: eq, lt
  Multiplexer #(.width(32), .enable("false")) multiplexer_17 (
    .in0(subtractor_9_out), .in1({multiplexer_9_out[30:0], multiplexer_10_out[31]}),
    .out(multiplexer_17_out), .sel(comparator_9_gt));
  Multiplexer #(.width(32), .enable("false")) multiplexer_18 (
    .in0(or_9_out), .in1({multiplexer_10_out[30:0], 1'b0}), .out(multiplexer_18_out), .sel(comparator_9_gt));
  Multiplexer #(.width(32), .enable("false")) multiplexer_19 (
    .in0(subtractor_10_out), .in1({multiplexer_11_out[30:0], multiplexer_12_out[31]}),
    .out(multiplexer_19_out), .sel(comparator_10_gt));
  Multiplexer #(.width(32), .enable("false")) multiplexer_20 (
    .in0(or_10_out), .in1({multiplexer_12_out[30:0], 1'b0}), .out(multiplexer_20_out), .sel(comparator_10_gt));
  Subtractor #(.width(32)) subtractor_11 (
    .a({multiplexer_13_out[30:0], multiplexer_14_out[31]}), .b(d_31_0), .out(subtractor_11_out), .bin(1'b0));  // open: bout
  assign or_11_out = 32'h1 | {multiplexer_14_out[30:0], 1'b0};  // OR_Gate or_11, 32 bits wide
  Comparator #(.width(32), .mode("unsigned")) comparator_12 (
    .a(d_31_0), .b({multiplexer_15_out[30:0], multiplexer_16_out[31]}), .gt(comparator_12_gt));  // open: eq, lt
  Multiplexer #(.width(32), .enable("false")) multiplexer_21 (
    .in0(subtractor_11_out), .in1({multiplexer_13_out[30:0], multiplexer_14_out[31]}),
    .out(multiplexer_21_out), .sel(comparator_11_gt));
  Multiplexer #(.width(32), .enable("false")) multiplexer_22 (
    .in0(or_11_out), .in1({multiplexer_14_out[30:0], 1'b0}), .out(multiplexer_22_out), .sel(comparator_11_gt));
  Subtractor #(.width(32)) subtractor_12 (
    .a({multiplexer_15_out[30:0], multiplexer_16_out[31]}), .b(d_31_0), .out(subtractor_12_out), .bin(1'b0));  // open: bout
  Multiplexer #(.width(32), .enable("false")) multiplexer_23 (
    .in0(subtractor_12_out), .in1({multiplexer_15_out[30:0], multiplexer_16_out[31]}),
    .out(multiplexer_23_out), .sel(comparator_12_gt));
  assign or_12_out = 32'h1 | {multiplexer_16_out[30:0], 1'b0};  // OR_Gate or_12, 32 bits wide
  Multiplexer #(.width(32), .enable("false")) multiplexer_24 (
    .in0(or_12_out), .in1({multiplexer_16_out[30:0], 1'b0}), .out(multiplexer_24_out), .sel(comparator_12_gt));
  Comparator #(.width(32), .mode("unsigned")) comparator_13 (
    .a(d_31_0), .b({multiplexer_17_out[30:0], multiplexer_18_out[31]}), .gt(comparator_13_gt));  // open: eq, lt
  Subtractor #(.width(32)) subtractor_13 (
    .a({multiplexer_17_out[30:0], multiplexer_18_out[31]}), .b(d_31_0), .out(subtractor_13_out), .bin(1'b0));  // open: bout
  Multiplexer #(.width(32), .enable("false")) multiplexer_25 (
    .in0(subtractor_13_out), .in1({multiplexer_17_out[30:0], multiplexer_18_out[31]}),
    .out(multiplexer_25_out), .sel(comparator_13_gt));
  assign or_13_out = 32'h1 | {multiplexer_18_out[30:0], 1'b0};  // OR_Gate or_13, 32 bits wide
  Multiplexer #(.width(32), .enable("false")) multiplexer_26 (
    .in0(or_13_out), .in1({multiplexer_18_out[30:0], 1'b0}), .out(multiplexer_26_out), .sel(comparator_13_gt));
  Comparator #(.width(32), .mode("unsigned")) comparator_14 (
    .a(d_31_0), .b({multiplexer_19_out[30:0], multiplexer_20_out[31]}), .gt(comparator_14_gt));  // open: eq, lt
  Subtractor #(.width(32)) subtractor_14 (
    .a({multiplexer_19_out[30:0], multiplexer_20_out[31]}), .b(d_31_0), .out(subtractor_14_out), .bin(1'b0));  // open: bout
  assign or_14_out = 32'h1 | {multiplexer_20_out[30:0], 1'b0};  // OR_Gate or_14, 32 bits wide
  Comparator #(.width(32), .mode("unsigned")) comparator_15 (
    .a(d_31_0), .b({multiplexer_21_out[30:0], multiplexer_22_out[31]}), .gt(comparator_15_gt));  // open: eq, lt
  Multiplexer #(.width(32), .enable("false")) multiplexer_27 (
    .in0(subtractor_14_out), .in1({multiplexer_19_out[30:0], multiplexer_20_out[31]}),
    .out(multiplexer_27_out), .sel(comparator_14_gt));
  Multiplexer #(.width(32), .enable("false")) multiplexer_28 (
    .in0(or_14_out), .in1({multiplexer_20_out[30:0], 1'b0}), .out(multiplexer_28_out), .sel(comparator_14_gt));
  Subtractor #(.width(32)) subtractor_15 (
    .a({multiplexer_21_out[30:0], multiplexer_22_out[31]}), .b(d_31_0), .out(subtractor_15_out), .bin(1'b0));  // open: bout
  assign or_15_out = 32'h1 | {multiplexer_22_out[30:0], 1'b0};  // OR_Gate or_15, 32 bits wide
  Comparator #(.width(32), .mode("unsigned")) comparator_16 (
    .a(d_31_0), .b({multiplexer_23_out[30:0], multiplexer_24_out[31]}), .gt(comparator_16_gt));  // open: eq, lt
  Subtractor #(.width(32)) subtractor_16 (
    .a({multiplexer_23_out[30:0], multiplexer_24_out[31]}), .b(d_31_0), .out(subtractor_16_out), .bin(1'b0));  // open: bout
  Multiplexer #(.width(32), .enable("false")) multiplexer_29 (
    .in0(subtractor_15_out), .in1({multiplexer_21_out[30:0], multiplexer_22_out[31]}),
    .out(multiplexer_29_out), .sel(comparator_15_gt));
  Multiplexer #(.width(32), .enable("false")) multiplexer_30 (
    .in0(or_15_out), .in1({multiplexer_22_out[30:0], 1'b0}), .out(multiplexer_30_out), .sel(comparator_15_gt));
  Multiplexer #(.width(32), .enable("false")) multiplexer_31 (
    .in0(subtractor_16_out), .in1({multiplexer_23_out[30:0], multiplexer_24_out[31]}),
    .out(multiplexer_31_out), .sel(comparator_16_gt));
  assign or_16_out = 32'h1 | {multiplexer_24_out[30:0], 1'b0};  // OR_Gate or_16, 32 bits wide
  Multiplexer #(.width(32), .enable("false")) multiplexer_32 (
    .in0(or_16_out), .in1({multiplexer_24_out[30:0], 1'b0}), .out(multiplexer_32_out), .sel(comparator_16_gt));
  Comparator #(.width(32), .mode("unsigned")) comparator_17 (
    .a(d_31_0), .b({multiplexer_25_out[30:0], multiplexer_26_out[31]}), .gt(comparator_17_gt));  // open: eq, lt
  Subtractor #(.width(32)) subtractor_17 (
    .a({multiplexer_25_out[30:0], multiplexer_26_out[31]}), .b(d_31_0), .out(subtractor_17_out), .bin(1'b0));  // open: bout
  Multiplexer #(.width(32), .enable("false")) multiplexer_33 (
    .in0(subtractor_17_out), .in1({multiplexer_25_out[30:0], multiplexer_26_out[31]}),
    .out(multiplexer_33_out), .sel(comparator_17_gt));
  assign or_17_out = 32'h1 | {multiplexer_26_out[30:0], 1'b0};  // OR_Gate or_17, 32 bits wide
  Multiplexer #(.width(32), .enable("false")) multiplexer_34 (
    .in0(or_17_out), .in1({multiplexer_26_out[30:0], 1'b0}), .out(multiplexer_34_out), .sel(comparator_17_gt));
  Comparator #(.width(32), .mode("unsigned")) comparator_18 (
    .a(d_31_0), .b({multiplexer_27_out[30:0], multiplexer_28_out[31]}), .gt(comparator_18_gt));  // open: eq, lt
  Subtractor #(.width(32)) subtractor_18 (
    .a({multiplexer_27_out[30:0], multiplexer_28_out[31]}), .b(d_31_0), .out(subtractor_18_out), .bin(1'b0));  // open: bout
  assign or_18_out = 32'h1 | {multiplexer_28_out[30:0], 1'b0};  // OR_Gate or_18, 32 bits wide
  Comparator #(.width(32), .mode("unsigned")) comparator_19 (
    .a(d_31_0), .b({multiplexer_29_out[30:0], multiplexer_30_out[31]}), .gt(comparator_19_gt));  // open: eq, lt
  Multiplexer #(.width(32), .enable("false")) multiplexer_35 (
    .in0(subtractor_18_out), .in1({multiplexer_27_out[30:0], multiplexer_28_out[31]}),
    .out(multiplexer_35_out), .sel(comparator_18_gt));
  Multiplexer #(.width(32), .enable("false")) multiplexer_36 (
    .in0(or_18_out), .in1({multiplexer_28_out[30:0], 1'b0}), .out(multiplexer_36_out), .sel(comparator_18_gt));
  Subtractor #(.width(32)) subtractor_19 (
    .a({multiplexer_29_out[30:0], multiplexer_30_out[31]}), .b(d_31_0), .out(subtractor_19_out), .bin(1'b0));  // open: bout
  assign or_19_out = 32'h1 | {multiplexer_30_out[30:0], 1'b0};  // OR_Gate or_19, 32 bits wide
  Comparator #(.width(32), .mode("unsigned")) comparator_20 (
    .a(d_31_0), .b({multiplexer_31_out[30:0], multiplexer_32_out[31]}), .gt(comparator_20_gt));  // open: eq, lt
  Subtractor #(.width(32)) subtractor_20 (
    .a({multiplexer_31_out[30:0], multiplexer_32_out[31]}), .b(d_31_0), .out(subtractor_20_out), .bin(1'b0));  // open: bout
  assign or_20_out = 32'h1 | {multiplexer_32_out[30:0], 1'b0};  // OR_Gate or_20, 32 bits wide
  Multiplexer #(.width(32), .enable("false")) multiplexer_37 (
    .in0(subtractor_19_out), .in1({multiplexer_29_out[30:0], multiplexer_30_out[31]}),
    .out(multiplexer_37_out), .sel(comparator_19_gt));
  Multiplexer #(.width(32), .enable("false")) multiplexer_38 (
    .in0(or_19_out), .in1({multiplexer_30_out[30:0], 1'b0}), .out(multiplexer_38_out), .sel(comparator_19_gt));
  Multiplexer #(.width(32), .enable("false")) multiplexer_39 (
    .in0(subtractor_20_out), .in1({multiplexer_31_out[30:0], multiplexer_32_out[31]}),
    .out(multiplexer_39_out), .sel(comparator_20_gt));
  Multiplexer #(.width(32), .enable("false")) multiplexer_40 (
    .in0(or_20_out), .in1({multiplexer_32_out[30:0], 1'b0}), .out(multiplexer_40_out), .sel(comparator_20_gt));
  Comparator #(.width(32), .mode("unsigned")) comparator_21 (
    .a(d_31_0), .b({multiplexer_33_out[30:0], multiplexer_34_out[31]}), .gt(comparator_21_gt));  // open: eq, lt
  Subtractor #(.width(32)) subtractor_21 (
    .a({multiplexer_33_out[30:0], multiplexer_34_out[31]}), .b(d_31_0), .out(subtractor_21_out), .bin(1'b0));  // open: bout
  assign or_21_out = 32'h1 | {multiplexer_34_out[30:0], 1'b0};  // OR_Gate or_21, 32 bits wide
  Comparator #(.width(32), .mode("unsigned")) comparator_22 (
    .a(d_31_0), .b({multiplexer_35_out[30:0], multiplexer_36_out[31]}), .gt(comparator_22_gt));  // open: eq, lt
  Multiplexer #(.width(32), .enable("false")) multiplexer_41 (
    .in0(subtractor_21_out), .in1({multiplexer_33_out[30:0], multiplexer_34_out[31]}),
    .out(multiplexer_41_out), .sel(comparator_21_gt));
  Multiplexer #(.width(32), .enable("false")) multiplexer_42 (
    .in0(or_21_out), .in1({multiplexer_34_out[30:0], 1'b0}), .out(multiplexer_42_out), .sel(comparator_21_gt));
  Subtractor #(.width(32)) subtractor_22 (
    .a({multiplexer_35_out[30:0], multiplexer_36_out[31]}), .b(d_31_0), .out(subtractor_22_out), .bin(1'b0));  // open: bout
  assign or_22_out = 32'h1 | {multiplexer_36_out[30:0], 1'b0};  // OR_Gate or_22, 32 bits wide
  Comparator #(.width(32), .mode("unsigned")) comparator_23 (
    .a(d_31_0), .b({multiplexer_37_out[30:0], multiplexer_38_out[31]}), .gt(comparator_23_gt));  // open: eq, lt
  Subtractor #(.width(32)) subtractor_23 (
    .a({multiplexer_37_out[30:0], multiplexer_38_out[31]}), .b(d_31_0), .out(subtractor_23_out), .bin(1'b0));  // open: bout
  Multiplexer #(.width(32), .enable("false")) multiplexer_43 (
    .in0(subtractor_22_out), .in1({multiplexer_35_out[30:0], multiplexer_36_out[31]}),
    .out(multiplexer_43_out), .sel(comparator_22_gt));
  Multiplexer #(.width(32), .enable("false")) multiplexer_44 (
    .in0(or_22_out), .in1({multiplexer_36_out[30:0], 1'b0}), .out(multiplexer_44_out), .sel(comparator_22_gt));
  Multiplexer #(.width(32), .enable("false")) multiplexer_45 (
    .in0(subtractor_23_out), .in1({multiplexer_37_out[30:0], multiplexer_38_out[31]}),
    .out(multiplexer_45_out), .sel(comparator_23_gt));
  assign or_23_out = 32'h1 | {multiplexer_38_out[30:0], 1'b0};  // OR_Gate or_23, 32 bits wide
  Multiplexer #(.width(32), .enable("false")) multiplexer_46 (
    .in0(or_23_out), .in1({multiplexer_38_out[30:0], 1'b0}), .out(multiplexer_46_out), .sel(comparator_23_gt));
  Comparator #(.width(32), .mode("unsigned")) comparator_24 (
    .a(d_31_0), .b({multiplexer_39_out[30:0], multiplexer_40_out[31]}), .gt(comparator_24_gt));  // open: eq, lt
  Subtractor #(.width(32)) subtractor_24 (
    .a({multiplexer_39_out[30:0], multiplexer_40_out[31]}), .b(d_31_0), .out(subtractor_24_out), .bin(1'b0));  // open: bout
  assign or_24_out = 32'h1 | {multiplexer_40_out[30:0], 1'b0};  // OR_Gate or_24, 32 bits wide
  Multiplexer #(.width(32), .enable("false")) multiplexer_47 (
    .in0(subtractor_24_out), .in1({multiplexer_39_out[30:0], multiplexer_40_out[31]}),
    .out(multiplexer_47_out), .sel(comparator_24_gt));
  Multiplexer #(.width(32), .enable("false")) multiplexer_48 (
    .in0(or_24_out), .in1({multiplexer_40_out[30:0], 1'b0}), .out(multiplexer_48_out), .sel(comparator_24_gt));
  Comparator #(.width(32), .mode("unsigned")) comparator_25 (
    .a(d_31_0), .b({multiplexer_41_out[30:0], multiplexer_42_out[31]}), .gt(comparator_25_gt));  // open: eq, lt
  Subtractor #(.width(32)) subtractor_25 (
    .a({multiplexer_41_out[30:0], multiplexer_42_out[31]}), .b(d_31_0), .out(subtractor_25_out), .bin(1'b0));  // open: bout
  assign or_25_out = 32'h1 | {multiplexer_42_out[30:0], 1'b0};  // OR_Gate or_25, 32 bits wide
  Comparator #(.width(32), .mode("unsigned")) comparator_26 (
    .a(d_31_0), .b({multiplexer_43_out[30:0], multiplexer_44_out[31]}), .gt(comparator_26_gt));  // open: eq, lt
  Subtractor #(.width(32)) subtractor_26 (
    .a({multiplexer_43_out[30:0], multiplexer_44_out[31]}), .b(d_31_0), .out(subtractor_26_out), .bin(1'b0));  // open: bout
  Multiplexer #(.width(32), .enable("false")) multiplexer_49 (
    .in0(subtractor_25_out), .in1({multiplexer_41_out[30:0], multiplexer_42_out[31]}),
    .out(multiplexer_49_out), .sel(comparator_25_gt));
  Multiplexer #(.width(32), .enable("false")) multiplexer_50 (
    .in0(or_25_out), .in1({multiplexer_42_out[30:0], 1'b0}), .out(multiplexer_50_out), .sel(comparator_25_gt));
  Multiplexer #(.width(32), .enable("false")) multiplexer_51 (
    .in0(subtractor_26_out), .in1({multiplexer_43_out[30:0], multiplexer_44_out[31]}),
    .out(multiplexer_51_out), .sel(comparator_26_gt));
  assign or_26_out = 32'h1 | {multiplexer_44_out[30:0], 1'b0};  // OR_Gate or_26, 32 bits wide
  Multiplexer #(.width(32), .enable("false")) multiplexer_52 (
    .in0(or_26_out), .in1({multiplexer_44_out[30:0], 1'b0}), .out(multiplexer_52_out), .sel(comparator_26_gt));
  Comparator #(.width(32), .mode("unsigned")) comparator_27 (
    .a(d_31_0), .b({multiplexer_45_out[30:0], multiplexer_46_out[31]}), .gt(comparator_27_gt));  // open: eq, lt
  Subtractor #(.width(32)) subtractor_27 (
    .a({multiplexer_45_out[30:0], multiplexer_46_out[31]}), .b(d_31_0), .out(subtractor_27_out), .bin(1'b0));  // open: bout
  assign or_27_out = 32'h1 | {multiplexer_46_out[30:0], 1'b0};  // OR_Gate or_27, 32 bits wide
  Comparator #(.width(32), .mode("unsigned")) comparator_28 (
    .a(d_31_0), .b({multiplexer_47_out[30:0], multiplexer_48_out[31]}), .gt(comparator_28_gt));  // open: eq, lt
  Multiplexer #(.width(32), .enable("false")) multiplexer_53 (
    .in0(subtractor_27_out), .in1({multiplexer_45_out[30:0], multiplexer_46_out[31]}),
    .out(multiplexer_53_out), .sel(comparator_27_gt));
  Multiplexer #(.width(32), .enable("false")) multiplexer_54 (
    .in0(or_27_out), .in1({multiplexer_46_out[30:0], 1'b0}), .out(multiplexer_54_out), .sel(comparator_27_gt));
  Subtractor #(.width(32)) subtractor_28 (
    .a({multiplexer_47_out[30:0], multiplexer_48_out[31]}), .b(d_31_0), .out(subtractor_28_out), .bin(1'b0));  // open: bout
  assign or_28_out = 32'h1 | {multiplexer_48_out[30:0], 1'b0};  // OR_Gate or_28, 32 bits wide
  Multiplexer #(.width(32), .enable("false")) multiplexer_55 (
    .in0(subtractor_28_out), .in1({multiplexer_47_out[30:0], multiplexer_48_out[31]}),
    .out(multiplexer_55_out), .sel(comparator_28_gt));
  Multiplexer #(.width(32), .enable("false")) multiplexer_56 (
    .in0(or_28_out), .in1({multiplexer_48_out[30:0], 1'b0}), .out(multiplexer_56_out), .sel(comparator_28_gt));
  Comparator #(.width(32), .mode("unsigned")) comparator_29 (
    .a(d_31_0), .b({multiplexer_49_out[30:0], multiplexer_50_out[31]}), .gt(comparator_29_gt));  // open: eq, lt
  Subtractor #(.width(32)) subtractor_29 (
    .a({multiplexer_49_out[30:0], multiplexer_50_out[31]}), .b(d_31_0), .out(subtractor_29_out), .bin(1'b0));  // open: bout
  assign or_29_out = 32'h1 | {multiplexer_50_out[30:0], 1'b0};  // OR_Gate or_29, 32 bits wide
  Comparator #(.width(32), .mode("unsigned")) comparator_30 (
    .a(d_31_0), .b({multiplexer_51_out[30:0], multiplexer_52_out[31]}), .gt(comparator_30_gt));  // open: eq, lt
  Subtractor #(.width(32)) subtractor_30 (
    .a({multiplexer_51_out[30:0], multiplexer_52_out[31]}), .b(d_31_0), .out(subtractor_30_out), .bin(1'b0));  // open: bout
  assign or_30_out = 32'h1 | {multiplexer_52_out[30:0], 1'b0};  // OR_Gate or_30, 32 bits wide
  Comparator #(.width(32), .mode("unsigned")) comparator_31 (
    .a(d_31_0), .b({multiplexer_53_out[30:0], multiplexer_54_out[31]}), .gt(comparator_31_gt));  // open: eq, lt
  Multiplexer #(.width(32), .enable("false")) multiplexer_57 (
    .in0(subtractor_29_out), .in1({multiplexer_49_out[30:0], multiplexer_50_out[31]}),
    .out(multiplexer_57_out), .sel(comparator_29_gt));
  Multiplexer #(.width(32), .enable("false")) multiplexer_58 (
    .in0(or_29_out), .in1({multiplexer_50_out[30:0], 1'b0}), .out(multiplexer_58_out), .sel(comparator_29_gt));
  Multiplexer #(.width(32), .enable("false")) multiplexer_59 (
    .in0(subtractor_30_out), .in1({multiplexer_51_out[30:0], multiplexer_52_out[31]}),
    .out(multiplexer_59_out), .sel(comparator_30_gt));
  Multiplexer #(.width(32), .enable("false")) multiplexer_60 (
    .in0(or_30_out), .in1({multiplexer_52_out[30:0], 1'b0}), .out(multiplexer_60_out), .sel(comparator_30_gt));
  Subtractor #(.width(32)) subtractor_31 (
    .a({multiplexer_53_out[30:0], multiplexer_54_out[31]}), .b(d_31_0), .out(subtractor_31_out), .bin(1'b0));  // open: bout
  assign or_31_out = 32'h1 | {multiplexer_54_out[30:0], 1'b0};  // OR_Gate or_31, 32 bits wide
  Comparator #(.width(32), .mode("unsigned")) comparator_32 (
    .a(d_31_0), .b({multiplexer_55_out[30:0], multiplexer_56_out[31]}), .gt(comparator_32_gt));  // open: eq, lt
  Multiplexer #(.width(32), .enable("false")) multiplexer_61 (
    .in0(subtractor_31_out), .in1({multiplexer_53_out[30:0], multiplexer_54_out[31]}),
    .out(multiplexer_61_out), .sel(comparator_31_gt));
  Multiplexer #(.width(32), .enable("false")) multiplexer_62 (
    .in0(or_31_out), .in1({multiplexer_54_out[30:0], 1'b0}), .out(multiplexer_62_out), .sel(comparator_31_gt));
  Subtractor #(.width(32)) subtractor_32 (
    .a({multiplexer_55_out[30:0], multiplexer_56_out[31]}), .b(d_31_0), .out(subtractor_32_out), .bin(1'b0));  // open: bout
  Multiplexer #(.width(32), .enable("false")) multiplexer_63 (
    .in0(subtractor_32_out), .in1({multiplexer_55_out[30:0], multiplexer_56_out[31]}), .out(rem_31_0),
    .sel(comparator_32_gt));
  assign or_32_out = 32'h1 | {multiplexer_56_out[30:0], 1'b0};  // OR_Gate or_32, 32 bits wide
  Multiplexer #(.width(32), .enable("false")) multiplexer_64 (
    .in0(or_32_out), .in1({multiplexer_56_out[30:0], 1'b0}), .out(quot_31_0), .sel(comparator_32_gt));
endmodule

module \_32位除法器测试电路  (
  input  [31:0] \被除数 ,
  input  [31:0] \除数 ,
  output [31:0] \商 ,
  output [31:0] \余数 
);

  \_32位除法器  \u_32位除法器_1  (.d_31_0(\除数 ), .n_31_0(\被除数 ), .rem_31_0(\余数 ), .quot_31_0(\商 ));
endmodule
