// Logisim project 实验5-CS1906-U201915115-郑舟.circ as structural Verilog: 14 circuits, main circuit 四位二进制可逆计数器
module \四位二进制可逆计数器  (
  input  CLR,
  input  nLR,
  input  A,
  input  B,
  input  C,
  input  D,
  input  CPU,
  input  CPD,
  output QA,
  output QB,
  output QC,
  output QD
);

  wire and_1_out, and_2_out, and_3_out, and_4_out, and_5_out, and_6_out, and_7_out, and_8_out, and_9_out,
       and_10_out, and_11_out, and_12_out, and_13_out, and_14_out, d_ff_1_qn, d_ff_2_qn, d_ff_3_qn,
       d_ff_4_qn, not_1_out, not_2_out, not_3_out, not_4_out, not_5_out, or_1_out, or_2_out, or_3_out,
       or_4_out, or_5_out, or_6_out, or_7_out, or_8_out;

  not not_1 (not_1_out, nLR);
  not not_2 (not_2_out, A);
  not not_3 (not_3_out, B);
  not not_4 (not_4_out, C);
  not not_5 (not_5_out, D);
  and and_1 (and_1_out, not_2_out, not_1_out);
  and and_2 (and_2_out, not_3_out, not_1_out);
  and and_3 (and_3_out, not_4_out, not_1_out);
  and and_4 (and_4_out, not_5_out, not_1_out);
  and and_5 (and_5_out, not_1_out, A);
  and and_6 (and_6_out, not_1_out, B);
  and and_7 (and_7_out, not_1_out, C);
  and and_8 (and_8_out, not_1_out, D);
  or or_1 (or_1_out, CPU, CPD);
  and and_9 (and_9_out, CPU, QA);
  or or_2 (or_2_out, and_9_out, and_10_out);
  and and_10 (and_10_out, CPD, d_ff_1_qn);
  and and_11 (and_11_out, CPU, QA, QB);
  or or_3 (or_3_out, and_11_out, and_12_out);
  and and_12 (and_12_out, CPD, d_ff_1_qn, d_ff_2_qn);
  and and_13 (and_13_out, CPU, QC, QB, QA);
  or or_4 (or_4_out, and_13_out, and_14_out);
  and and_14 (and_14_out, CPD, d_ff_1_qn, d_ff_2_qn, d_ff_3_qn);
  or or_5 (or_5_out, CLR, and_1_out);
  or or_6 (or_6_out, CLR, and_2_out);
  or or_7 (or_7_out, CLR, and_3_out);
  or or_8 (or_8_out, CLR, and_4_out);
  D_Flip_Flop #(.trigger("falling")) d_ff_1 (
    .clk(or_1_out), .D(d_ff_1_qn), .Q(QA), .Qn(d_ff_1_qn), .preset(and_5_out), .reset(or_5_out));
  D_Flip_Flop #(.trigger("falling")) d_ff_2 (
    .clk(or_2_out), .D(d_ff_2_qn), .Q(QB), .Qn(d_ff_2_qn), .preset(and_6_out), .reset(or_6_out));
  D_Flip_Flop #(.trigger("falling")) d_ff_3 (
    .clk(or_3_out), .D(d_ff_3_qn), .Q(QC), .Qn(d_ff_3_qn), .preset(and_7_out), .reset(or_7_out));
  D_Flip_Flop #(.trigger("falling")) d_ff_4 (
    .clk(or_4_out), .D(d_ff_4_qn), .Q(QD), .Qn(d_ff_4_qn), .preset(and_8_out), .reset(or_8_out));
endmodule

module \六十进制计数器  (
  input  CPU,
  input  CLR,
  input  CPD,
  input  Adj,
  output Q0D,
  output Q0C,
  output Q0B,
  output Q0A,
  output Q1D,
  output Q1C,
  output Q1B,
  output Q1A,
  output nQCC
);

  wire and_1_out, and_2_out, and_3_out, and_4_out, and_5_out, and_6_out, not_1_out, or_1_out, or_2_out,
       or_3_out, or_4_out, or_5_out;

  and and_1 (and_1_out, CPD, Adj);
  or or_1 (or_1_out, and_4_out, CLR);
  or or_2 (or_2_out, or_4_out, or_3_out);
  or or_3 (or_3_out, Q0D, Q0C, Q0B, Q0A);
  and and_2 (and_2_out, or_2_out, and_1_out);
  \四位二进制可逆计数器  \u_四位二进制可逆计数器_1  (
    .CLR(or_1_out), .nLR(not_1_out), .A(1'b1), .B(1'b0), .C(1'b0), .D(1'b1), .QA(Q0A), .QB(Q0B), .QC(Q0C),
    .QD(Q0D), .CPU(CPU), .CPD(and_2_out));
  and and_3 (and_3_out, Q0D, Q0C, Q0B, Q0A);
  not not_1 (not_1_out, and_3_out);
  and and_4 (and_4_out, Q0D, ~Q0C, Q0B, ~Q0A);  // AND_Gate
  and and_5 (and_5_out, or_4_out, and_3_out);
  or or_4 (or_4_out, Q1D, Q1C, Q1B, Q1A);
  or or_5 (or_5_out, and_6_out, CLR);
  and and_6 (and_6_out, ~Q1D, Q1C, Q1B, ~Q1A);  // AND_Gate
  \四位二进制可逆计数器  \u_四位二进制可逆计数器_2  (
    .CLR(or_5_out), .nLR(1'b1), .A(1'b1), .B(1'b1), .C(1'b1), .D(1'b1), .QA(Q1A), .QB(Q1B), .QC(Q1C),
    .QD(Q1D), .CPU(and_4_out), .CPD(and_5_out));
  and and_7 (nQCC, and_6_out, ~Adj);  // AND_Gate
endmodule

module \六十进制计数器测试电路  (
  input  in_1,
  input  in_2
);

  wire button_1_out, button_2_out, t_ff_1_q, \六十进制计数器_1_nqcc ;
  wire [3:0] \六十进制计数器_1_q0a , \六十进制计数器_1_q1a ;

  Button button_1 (.out(button_1_out));
  Button button_2 (.out(button_2_out));
  Hex_Digit_Display hex_digit_display_1 (.value(\六十进制计数器_1_q1a ), .dp(1'b0));
  Hex_Digit_Display hex_digit_display_2 (.value(\六十进制计数器_1_q0a ), .dp(1'b0));
  \六十进制计数器  \u_六十进制计数器_1  (
    .CPU(button_1_out), .CLR(in_2), .CPD(button_2_out), .Adj(in_1), .nQCC(\六十进制计数器_1_nqcc ),
    .Q0D(\六十进制计数器_1_q0a [3]), .Q0C(\六十进制计数器_1_q0a [2]), .Q0B(\六十进制计数器_1_q0a [1]), .Q0A(\六十进制计数器_1_q0a [0]),
    .Q1D(\六十进制计数器_1_q1a [3]), .Q1C(\六十进制计数器_1_q1a [2]), .Q1B(\六十进制计数器_1_q1a [1]), .Q1A(\六十进制计数器_1_q1a [0]));
  LED led_1 (.in(t_ff_1_q));
  T_Flip_Flop #(.trigger("falling"), .Pre_Clr_Positions("LEGACY")) t_ff_1 (
    .clk(\六十进制计数器_1_nqcc ), .T(1'b1), .Q(t_ff_1_q), .preset(1'b0), .reset(1'b0));  // open: Qn
endmodule

module \十二进制计数器或二十四进制的计数器电路  (
  input  CPU,
  input  Adj,
  input  CPD,
  input  Clr,
  input  Set,
  output Q1D,
  output Q1C,
  output Q1B,
  output Q1A,
  output Q0D,
  output Q0C,
  output Q0B,
  output Q0A,
  output nQCC
);

  wire and_1_out, and_2_out, or_1_out;

  \六十进制计数器  \u_六十进制计数器_1  (
    .CPU(CPU), .CLR(or_1_out), .CPD(CPD), .Adj(Adj), .Q0D(Q0D), .Q0C(Q0C), .Q0B(Q0B), .Q0A(Q0A), .Q1D(Q1D),
    .Q1C(Q1C), .Q1B(Q1B), .Q1A(Q1A));  // open: nQCC
  or or_1 (or_1_out, nQCC, Clr);
  and and_1 (and_1_out, ~Q1B, Q1A, ~Q0D, ~Q0C, Q0B, ~Q0A);  // AND_Gate
  and and_2 (and_2_out, Q1B, ~Q1A, ~Q0D, Q0C, ~Q0B, ~Q0A);  // AND_Gate
  Multiplexer #(.enable("false")) multiplexer_1 (.in0(and_1_out), .in1(and_2_out), .out(nQCC), .sel(Set));
endmodule

module \十二或二十四进制的计数器测试电路  (
  input  in_1,
  input  in_2,
  input  in_3
);

  wire button_1_out, button_2_out, t_ff_1_q, \十二进制计数器或二十四进制的计数器电路_1_nqcc ;
  wire [3:0] \十二进制计数器或二十四进制的计数器电路_1_q0a , \十二进制计数器或二十四进制的计数器电路_1_q1a ;

  Button button_1 (.out(button_1_out));
  Button button_2 (.out(button_2_out));
  Hex_Digit_Display hex_digit_display_1 (.value(\十二进制计数器或二十四进制的计数器电路_1_q1a ), .dp(1'b0));
  Hex_Digit_Display hex_digit_display_2 (.value(\十二进制计数器或二十四进制的计数器电路_1_q0a ), .dp(1'b0));
  \十二进制计数器或二十四进制的计数器电路  \u_十二进制计数器或二十四进制的计数器电路_1  (
    .CPU(button_1_out), .Adj(in_1), .CPD(button_2_out), .Clr(in_2), .Set(in_3),
    .nQCC(\十二进制计数器或二十四进制的计数器电路_1_nqcc ), .Q1B(\十二进制计数器或二十四进制的计数器电路_1_q1a [1]),
    .Q1A(\十二进制计数器或二十四进制的计数器电路_1_q1a [0]), .Q0D(\十二进制计数器或二十四进制的计数器电路_1_q0a [3]),
    .Q0C(\十二进制计数器或二十四进制的计数器电路_1_q0a [2]), .Q0B(\十二进制计数器或二十四进制的计数器电路_1_q0a [1]),
    .Q0A(\十二进制计数器或二十四进制的计数器电路_1_q0a [0]), .Q1D(\十二进制计数器或二十四进制的计数器电路_1_q1a [3]),
    .Q1C(\十二进制计数器或二十四进制的计数器电路_1_q1a [2]));
  LED led_1 (.in(t_ff_1_q));
  T_Flip_Flop #(.Pre_Clr_Positions("LEGACY")) t_ff_1 (
    .clk(\十二进制计数器或二十四进制的计数器电路_1_nqcc ), .T(1'b1), .Q(t_ff_1_q), .preset(1'b0), .reset(1'b0));  // open: Qn
endmodule

module \上下午文字显示电路  (
  input  AM_FM,
  input  TT,
  output [4:0] out_3,
  output [4:0] out_4,
  output [4:0] out_5,
  output [4:0] out_6
);

  wire [19:0] multiplexer_1_out;

  Multiplexer #(.width(20), .enable("false")) multiplexer_1 (
    .in0(20'hfca1), .in1(20'h87e90), .out(multiplexer_1_out), .sel(AM_FM));
  Multiplexer #(.width(20), .enable("false")) multiplexer_2 (
    .in0({20{1'b0}}), .in1(multiplexer_1_out), .out({out_3, out_4, out_5, out_6}), .sel(TT));
endmodule

module \上下午文字显示测试电路  (
  input  in_1,
  input  in_2
);

  wire [4:0] \上下午文字显示电路_1_out_3 , \上下午文字显示电路_1_out_4 , \上下午文字显示电路_1_out_5 , \上下午文字显示电路_1_out_6 ;

  DotMatrix #(.matrixcols(4), .matrixrows(5)) dotmatrix_1 (
    .col0(\上下午文字显示电路_1_out_3 ), .col1(\上下午文字显示电路_1_out_4 ), .col2(\上下午文字显示电路_1_out_5 ),
    .col3(\上下午文字显示电路_1_out_6 ));
  \上下午文字显示电路  \u_上下午文字显示电路_1  (
    .AM_FM(in_1), .TT(in_2), .out_3(\上下午文字显示电路_1_out_3 ), .out_4(\上下午文字显示电路_1_out_4 ),
    .out_5(\上下午文字显示电路_1_out_5 ), .out_6(\上下午文字显示电路_1_out_6 ));
endmodule

module \电子钟整点报时电路  (
  input  [3:0] H_high,
  input  [3:0] H_low,
  input  [3:0] Min_high,
  input  [3:0] Min_low,
  output nQCC
);

  wire comparator_1_lt, comparator_2_lt, comparator_3_lt;

  Comparator #(.width(4)) comparator_1 (.a(H_high), .b(4'b0101), .lt(comparator_1_lt));  // open: gt, eq
  Comparator #(.width(4), .mode("unsigned")) comparator_2 (
    .a(H_low), .b(4'b1001), .lt(comparator_2_lt));  // open: gt, eq
  Comparator #(.width(4)) comparator_3 (.a(Min_high), .b(4'b0101), .lt(comparator_3_lt));  // open: gt, eq
  and and_1 (nQCC, ~comparator_1_lt, ~comparator_2_lt, ~comparator_3_lt);  // AND_Gate
endmodule

module \电子钟整点报时电路测试电路  (
  input  [3:0] in_1,
  input  [3:0] in_2,
  input  [3:0] in_3,
  input  [3:0] in_4
);

  wire \电子钟整点报时电路_1_nqcc ;

  LED led_1 (.in(\电子钟整点报时电路_1_nqcc ));
  \电子钟整点报时电路  \u_电子钟整点报时电路_1  (.H_high(in_1), .H_low(in_2), .Min_high(in_3), .Min_low(in_4), .nQCC(\电子钟整点报时电路_1_nqcc ));
endmodule

module \秒计时脉冲产生电路  (
  input  p,
  output nQCC
);

  \四位二进制可逆计数器  \u_四位二进制可逆计数器_1  (
    .CLR(nQCC), .nLR(1'b1), .A(1'b0), .B(1'b0), .C(1'b0), .D(1'b0), .QD(nQCC), .CPU(p), .CPD(1'b0));  // open: QA, QB, QC
endmodule

module \多功能数字钟电路  (
  input  Alarm,
  input  Adj0,
  input  Adj1,
  input  CP,
  input  CPU,
  input  CPD,
  input  Set,
  input  Clr,
  output \整点报时 ,
  output [3:0] H_h,
  output [3:0] H_l,
  output [3:0] Min_h,
  output [3:0] Min_l,
  output [3:0] Sec_h,
  output [3:0] Sec_l,
  output \闹钟 ,
  output [4:0] L_15_19,
  output [4:0] L_10_14,
  output [4:0] L_5_9,
  output [4:0] L_0_4
);

  wire and_1_out, and_2_out, and_3_out, and_4_out, and_5_out, and_6_out, and_7_out, and_8_out, and_9_out,
       and_10_out, and_11_out, and_12_out, and_13_out, and_14_out, and_15_out, and_16_out, comparator_1_gt,
       not_1_out, not_2_out, or_1_out, or_2_out, \六十进制计数器_1_nqcc , \六十进制计数器_2_nqcc , \秒计时脉冲产生电路_1_nqcc ;
  wire [3:0] bit_extender_3_out, bit_extender_4_out, multiplexer_5_out, multiplexer_7_out, multiplexer_8_out,
       multiplexer_9_out, \六十进制计数器_1_q0a , \六十进制计数器_1_q1a , \六十进制计数器_2_q0a , \六十进制计数器_2_q1a ,
       \闹钟_1_h_h_alarm , \闹钟_1_h_l_alrm , \闹钟_1_min_h_alarm , \闹钟_1_min_l_alarm ;
  wire [4:0] adder_1_out, bit_extender_1_out, bit_extender_2_out, divider_1_out, divider_1_rem,
       multiplier_1_out, subtractor_1_out, \上下午文字显示电路_1_out_3 , \上下午文字显示电路_1_out_4 , \上下午文字显示电路_1_out_5 ,
       \上下午文字显示电路_1_out_6 , \闹钟_1_l_0_4 , \闹钟_1_l_5_9 , \闹钟_1_l_10_14 , \闹钟_1_l_15_19 ;
  wire [7:0] \十二进制计数器或二十四进制的计数器电路_1_q0a ;

  assign bit_extender_1_out = {{1{1'b0}}, \十二进制计数器或二十四进制的计数器电路_1_q0a [3:0]};  // Bit_Extender bit_extender_1
  assign bit_extender_2_out = {{1{1'b0}}, \十二进制计数器或二十四进制的计数器电路_1_q0a [7:4]};  // Bit_Extender bit_extender_2
  Adder #(.width(5)) adder_1 (
    .a(bit_extender_1_out), .b(multiplier_1_out), .out(adder_1_out), .cin(1'b0));  // open: cout
  Multiplier #(.width(5)) multiplier_1 (
    .a(bit_extender_2_out), .b(5'b01010), .out(multiplier_1_out));  // open: cin, cout
  Subtractor #(.width(5)) subtractor_1 (
    .a(adder_1_out), .b(5'b01100), .out(subtractor_1_out), .bin(1'b0));  // open: bout
  Divider #(.width(5)) divider_1 (
    .a(subtractor_1_out), .b(5'b01010), .out(divider_1_out), .rem(divider_1_rem));  // open: upper
  Multiplexer #(.width(5), .enable("false")) multiplexer_1 (
    .in0(\上下午文字显示电路_1_out_3 ), .in1(\闹钟_1_l_15_19 ), .out(L_15_19), .sel(Alarm));
  Bit_Extender #(.in_width(5), .out_width(4), .\type ("zero")) bit_extender_3 (
    .in(divider_1_out), .out(bit_extender_3_out));
  Bit_Extender #(.in_width(5), .out_width(4), .\type ("zero")) bit_extender_4 (
    .in(divider_1_rem), .out(bit_extender_4_out));
  Multiplexer #(.width(5), .enable("false")) multiplexer_2 (
    .in0(\上下午文字显示电路_1_out_4 ), .in1(\闹钟_1_l_10_14 ), .out(L_10_14), .sel(Alarm));
  Multiplexer #(.width(5), .enable("false")) multiplexer_3 (
    .in0(\上下午文字显示电路_1_out_5 ), .in1(\闹钟_1_l_5_9 ), .out(L_5_9), .sel(Alarm));
  \上下午文字显示电路  \u_上下午文字显示电路_1  (
    .AM_FM(comparator_1_gt), .TT(not_1_out), .out_3(\上下午文字显示电路_1_out_3 ), .out_4(\上下午文字显示电路_1_out_4 ),
    .out_5(\上下午文字显示电路_1_out_5 ), .out_6(\上下午文字显示电路_1_out_6 ));
  not not_1 (not_1_out, Set);
  and and_1 (and_1_out, ~Alarm, Adj0);  // AND_Gate
  Multiplexer #(.width(5), .enable("false")) multiplexer_4 (
    .in0(\上下午文字显示电路_1_out_6 ), .in1(\闹钟_1_l_0_4 ), .out(L_0_4), .sel(Alarm));
  or or_1 (or_1_out, \六十进制计数器_1_nqcc , and_5_out);
  and and_2 (and_2_out, ~Alarm, Adj1);  // AND_Gate
  and and_3 (and_3_out, Alarm, Adj1);
  not not_2 (not_2_out, Alarm);
  Multiplexer #(.width(4), .enable("false")) multiplexer_5 (
    .in0(\十二进制计数器或二十四进制的计数器电路_1_q0a [7:4]), .in1(bit_extender_3_out), .out(multiplexer_5_out),
    .sel(comparator_1_gt));
  Multiplexer #(.width(4), .enable("false")) multiplexer_6 (
    .in0(multiplexer_7_out), .in1(\闹钟_1_h_h_alarm ), .out(H_h), .sel(Alarm));
  Multiplexer #(.width(4), .enable("false")) multiplexer_7 (
    .in0(multiplexer_5_out), .in1(\十二进制计数器或二十四进制的计数器电路_1_q0a [7:4]), .out(multiplexer_7_out), .sel(Set));
  Comparator comparator_1 (.a(\十二进制计数器或二十四进制的计数器电路_1_q0a ), .b(8'h12), .gt(comparator_1_gt));  // open: eq, lt
  and and_4 (and_4_out, and_2_out, and_6_out);
  and and_5 (and_5_out, ~and_2_out, and_6_out);  // AND_Gate
  and and_6 (and_6_out, and_1_out, and_7_out);
  and and_7 (and_7_out, ~Alarm, CPU);  // AND_Gate
  and and_8 (and_8_out, Alarm, CPU);
  Multiplexer #(.width(4), .enable("false")) multiplexer_8 (
    .in0(\十二进制计数器或二十四进制的计数器电路_1_q0a [3:0]), .in1(bit_extender_4_out), .out(multiplexer_8_out),
    .sel(comparator_1_gt));
  \十二进制计数器或二十四进制的计数器电路  \u_十二进制计数器或二十四进制的计数器电路_1  (
    .CPU(or_1_out), .Adj(and_1_out), .CPD(and_9_out), .Clr(and_15_out), .Set(1'b1),
    .Q1B(\十二进制计数器或二十四进制的计数器电路_1_q0a [5]), .Q1A(\十二进制计数器或二十四进制的计数器电路_1_q0a [4]),
    .Q0D(\十二进制计数器或二十四进制的计数器电路_1_q0a [3]), .Q0C(\十二进制计数器或二十四进制的计数器电路_1_q0a [2]),
    .Q0B(\十二进制计数器或二十四进制的计数器电路_1_q0a [1]), .Q0A(\十二进制计数器或二十四进制的计数器电路_1_q0a [0]),
    .Q1D(\十二进制计数器或二十四进制的计数器电路_1_q0a [7]), .Q1C(\十二进制计数器或二十四进制的计数器电路_1_q0a [6]));  // open: nQCC
  \秒计时脉冲产生电路  \u_秒计时脉冲产生电路_1  (.p(CP), .nQCC(\秒计时脉冲产生电路_1_nqcc ));
  and and_9 (and_9_out, ~and_2_out, and_10_out);  // AND_Gate
  and and_10 (and_10_out, and_1_out, and_11_out);
  and and_11 (and_11_out, ~Alarm, CPD);  // AND_Gate
  Multiplexer #(.width(4), .enable("false")) multiplexer_9 (
    .in0(multiplexer_8_out), .in1(\十二进制计数器或二十四进制的计数器电路_1_q0a [3:0]), .out(multiplexer_9_out), .sel(Set));
  and and_12 (and_12_out, ~and_1_out, \秒计时脉冲产生电路_1_nqcc );  // AND_Gate
  and and_13 (and_13_out, and_2_out, and_10_out);
  and and_14 (and_14_out, Alarm, CPD);
  Multiplexer #(.width(4), .enable("false")) multiplexer_10 (
    .in0(multiplexer_9_out), .in1(\闹钟_1_h_l_alrm ), .out(H_l), .sel(Alarm));
  \闹钟  \u_闹钟_1  (
    .H_h_R(\十二进制计数器或二十四进制的计数器电路_1_q0a [7:4]), .H_l_R(\十二进制计数器或二十四进制的计数器电路_1_q0a [3:0]),
    .Min_h_R(\六十进制计数器_1_q1a ), .Min_l_R(\六十进制计数器_1_q0a ), .s_h_R(\六十进制计数器_2_q1a ), .s_l_R(\六十进制计数器_2_q0a ),
    .en(not_2_out), .out_17(\闹钟 ), .L_15_19(\闹钟_1_l_15_19 ), .L_10_14(\闹钟_1_l_10_14 ), .L_5_9(\闹钟_1_l_5_9 ),
    .L_0_4(\闹钟_1_l_0_4 ), .Adj1(and_3_out), .CPU(and_8_out), .CPD(and_14_out), .Set(Set), .Clr(and_16_out),
    .H_h_Alarm(\闹钟_1_h_h_alarm ), .H_l_Alrm(\闹钟_1_h_l_alrm ), .Min_h_Alarm(\闹钟_1_min_h_alarm ),
    .Min_l_Alarm(\闹钟_1_min_l_alarm ));
  or or_2 (or_2_out, \六十进制计数器_2_nqcc , and_4_out);
  Multiplexer #(.width(4), .enable("false")) multiplexer_11 (
    .in0(\六十进制计数器_1_q1a ), .in1(\闹钟_1_min_h_alarm ), .out(Min_h), .sel(Alarm));
  \六十进制计数器  \u_六十进制计数器_1  (
    .CPU(or_2_out), .CLR(and_15_out), .CPD(and_13_out), .Adj(and_1_out), .nQCC(\六十进制计数器_1_nqcc ),
    .Q0D(\六十进制计数器_1_q0a [3]), .Q0C(\六十进制计数器_1_q0a [2]), .Q0B(\六十进制计数器_1_q0a [1]), .Q0A(\六十进制计数器_1_q0a [0]),
    .Q1D(\六十进制计数器_1_q1a [3]), .Q1C(\六十进制计数器_1_q1a [2]), .Q1B(\六十进制计数器_1_q1a [1]), .Q1A(\六十进制计数器_1_q1a [0]));
  and and_15 (and_15_out, ~Alarm, Clr);  // AND_Gate
  Multiplexer #(.width(4), .enable("false")) multiplexer_12 (
    .in0(\六十进制计数器_1_q0a ), .in1(\闹钟_1_min_l_alarm ), .out(Min_l), .sel(Alarm));
  \电子钟整点报时电路  \u_电子钟整点报时电路_1  (
    .H_high(\六十进制计数器_1_q1a ), .H_low(\六十进制计数器_1_q0a ), .Min_high(\六十进制计数器_2_q1a ), .Min_low(\六十进制计数器_2_q0a ),
    .nQCC(\整点报时 ));
  and and_16 (and_16_out, Alarm, Clr);
  Multiplexer #(.width(4), .enable("false")) multiplexer_13 (
    .in0(\六十进制计数器_2_q1a ), .in1(4'b0000), .out(Sec_h), .sel(Alarm));
  Multiplexer #(.width(4), .enable("false")) multiplexer_14 (
    .in0(\六十进制计数器_2_q0a ), .in1(4'b0000), .out(Sec_l), .sel(Alarm));
  \六十进制计数器  \u_六十进制计数器_2  (
    .CPU(and_12_out), .CLR(and_15_out), .CPD(1'b0), .Adj(1'b0), .nQCC(\六十进制计数器_2_nqcc ),
    .Q0D(\六十进制计数器_2_q0a [3]), .Q0C(\六十进制计数器_2_q0a [2]), .Q0B(\六十进制计数器_2_q0a [1]), .Q0A(\六十进制计数器_2_q0a [0]),
    .Q1D(\六十进制计数器_2_q1a [3]), .Q1C(\六十进制计数器_2_q1a [2]), .Q1B(\六十进制计数器_2_q1a [1]), .Q1A(\六十进制计数器_2_q1a [0]));
endmodule

module \多功能数字钟测试电路  (
  input  in_1,
  input  in_2,
  input  in_3,
  input  in_4
);

  wire button_1_out, button_2_out, button_3_out, clock_1_out, \多功能数字钟电路_1_整点报时 , \多功能数字钟电路_1_闹钟 ;
  wire [3:0] \多功能数字钟电路_1_h_h , \多功能数字钟电路_1_h_l , \多功能数字钟电路_1_min_h , \多功能数字钟电路_1_min_l , \多功能数字钟电路_1_sec_h ,
       \多功能数字钟电路_1_sec_l ;
  wire [4:0] \多功能数字钟电路_1_l_0_4 , \多功能数字钟电路_1_l_5_9 , \多功能数字钟电路_1_l_10_14 , \多功能数字钟电路_1_l_15_19 ;

  DotMatrix #(.matrixcols(4), .matrixrows(5)) dotmatrix_1 (
    .col0(\多功能数字钟电路_1_l_15_19 ), .col1(\多功能数字钟电路_1_l_10_14 ), .col2(\多功能数字钟电路_1_l_5_9 ),
    .col3(\多功能数字钟电路_1_l_0_4 ));
  Clock clock_1 (.out(clock_1_out));
  Hex_Digit_Display hex_digit_display_1 (.value(\多功能数字钟电路_1_h_l ), .dp(1'b0));
  Hex_Digit_Display hex_digit_display_2 (.value(\多功能数字钟电路_1_h_h ), .dp(1'b0));
  Button button_1 (.out(button_1_out));
  Button button_2 (.out(button_2_out));
  Hex_Digit_Display hex_digit_display_3 (.value(\多功能数字钟电路_1_min_l ), .dp(1'b0));
  Hex_Digit_Display hex_digit_display_4 (.value(\多功能数字钟电路_1_min_h ), .dp(1'b0));
  Button button_3 (.out(button_3_out));
  Hex_Digit_Display hex_digit_display_5 (.value(\多功能数字钟电路_1_sec_h ), .dp(1'b0));
  LED led_1 (.in(\多功能数字钟电路_1_闹钟 ));
  \多功能数字钟电路  \u_多功能数字钟电路_1  (
    .Min_h(\多功能数字钟电路_1_min_h ), .Min_l(\多功能数字钟电路_1_min_l ), .Sec_h(\多功能数字钟电路_1_sec_h ),
    .Sec_l(\多功能数字钟电路_1_sec_l ), .\整点报时 (\多功能数字钟电路_1_整点报时 ), .Adj0(in_2), .Adj1(in_3), .CP(clock_1_out),
    .CPU(button_1_out), .CPD(button_2_out), .Set(in_4), .Clr(button_3_out), .H_h(\多功能数字钟电路_1_h_h ),
    .H_l(\多功能数字钟电路_1_h_l ), .Alarm(in_1), .L_15_19(\多功能数字钟电路_1_l_15_19 ), .L_10_14(\多功能数字钟电路_1_l_10_14 ),
    .L_5_9(\多功能数字钟电路_1_l_5_9 ), .L_0_4(\多功能数字钟电路_1_l_0_4 ), .\闹钟 (\多功能数字钟电路_1_闹钟 ));
  LED led_2 (.in(\多功能数字钟电路_1_整点报时 ));
  Hex_Digit_Display hex_digit_display_6 (.value(\多功能数字钟电路_1_sec_l ), .dp(1'b0));
endmodule

module \闹钟  (
  input  en,
  input  [3:0] H_h_R,
  input  [3:0] H_l_R,
  input  [3:0] Min_h_R,
  input  [3:0] Min_l_R,
  input  [3:0] s_h_R,
  input  [3:0] s_l_R,
  input  Adj1,
  input  CPU,
  input  CPD,
  input  Set,
  input  Clr,
  output [3:0] H_h_Alarm,
  output [3:0] H_l_Alrm,
  output [3:0] Min_h_Alarm,
  output [3:0] Min_l_Alarm,
  output out_17,
  output [4:0] L_15_19,
  output [4:0] L_10_14,
  output [4:0] L_5_9,
  output [4:0] L_0_4
);

  wire and_1_out, and_2_out, and_3_out, and_4_out, and_5_out, and_6_out, and_7_out, comparator_1_gt,
       comparator_2_eq, comparator_3_eq, comparator_4_eq, comparator_5_eq, d_ff_1_q, d_ff_1_qn, not_1_out,
       not_2_out, or_1_out, or_2_out, \四位二进制可逆计数器_1_qa , \四位二进制可逆计数器_1_qb , \四位二进制可逆计数器_1_qc ,
       \四位二进制可逆计数器_1_qd ;
  wire [3:0] bit_extender_3_out, bit_extender_4_out, multiplexer_1_out, multiplexer_3_out;
  wire [4:0] adder_1_out, bit_extender_1_out, bit_extender_2_out, divider_1_out, divider_1_rem,
       multiplier_1_out, subtractor_1_out;
  wire [7:0] \十二进制计数器或二十四进制的计数器电路_1_q0a ;

  assign bit_extender_1_out = {{1{1'b0}}, \十二进制计数器或二十四进制的计数器电路_1_q0a [3:0]};  // Bit_Extender bit_extender_1
  assign bit_extender_2_out = {{1{1'b0}}, \十二进制计数器或二十四进制的计数器电路_1_q0a [7:4]};  // Bit_Extender bit_extender_2
  Adder #(.width(5)) adder_1 (
    .a(bit_extender_1_out), .b(multiplier_1_out), .out(adder_1_out), .cin(1'b0));  // open: cout
  Multiplier #(.width(5)) multiplier_1 (
    .a(bit_extender_2_out), .b(5'b01010), .out(multiplier_1_out));  // open: cin, cout
  Subtractor #(.width(5)) subtractor_1 (
    .a(adder_1_out), .b(5'b01100), .out(subtractor_1_out), .bin(1'b0));  // open: bout
  Divider #(.width(5)) divider_1 (
    .a(subtractor_1_out), .b(5'b01010), .out(divider_1_out), .rem(divider_1_rem));  // open: upper
  Bit_Extender #(.in_width(5), .out_width(4), .\type ("zero")) bit_extender_3 (
    .in(divider_1_out), .out(bit_extender_3_out));
  Bit_Extender #(.in_width(5), .out_width(4), .\type ("zero")) bit_extender_4 (
    .in(divider_1_rem), .out(bit_extender_4_out));
  \上下午文字显示电路  \u_上下午文字显示电路_1  (
    .AM_FM(comparator_1_gt), .TT(not_1_out), .out_3(L_15_19), .out_4(L_10_14), .out_5(L_5_9), .out_6(L_0_4));
  not not_1 (not_1_out, Set);
  Multiplexer #(.width(4), .enable("false")) multiplexer_1 (
    .in0(\十二进制计数器或二十四进制的计数器电路_1_q0a [7:4]), .in1(bit_extender_3_out), .out(multiplexer_1_out),
    .sel(comparator_1_gt));
  Multiplexer #(.width(4), .enable("false")) multiplexer_2 (
    .in0(multiplexer_1_out), .in1(\十二进制计数器或二十四进制的计数器电路_1_q0a [7:4]), .out(H_h_Alarm), .sel(Set));
  Comparator comparator_1 (.a(\十二进制计数器或二十四进制的计数器电路_1_q0a ), .b(8'h12), .gt(comparator_1_gt));  // open: eq, lt
  and and_1 (and_1_out, Adj1, CPU);
  and and_2 (and_2_out, ~Adj1, CPU);  // AND_Gate
  Multiplexer #(.width(4), .enable("false")) multiplexer_3 (
    .in0(\十二进制计数器或二十四进制的计数器电路_1_q0a [3:0]), .in1(bit_extender_4_out), .out(multiplexer_3_out),
    .sel(comparator_1_gt));
  \十二进制计数器或二十四进制的计数器电路  \u_十二进制计数器或二十四进制的计数器电路_1  (
    .CPU(and_2_out), .Adj(1'b1), .CPD(and_3_out), .Clr(Clr), .Set(1'b1),
    .Q1B(\十二进制计数器或二十四进制的计数器电路_1_q0a [5]), .Q1A(\十二进制计数器或二十四进制的计数器电路_1_q0a [4]),
    .Q0D(\十二进制计数器或二十四进制的计数器电路_1_q0a [3]), .Q0C(\十二进制计数器或二十四进制的计数器电路_1_q0a [2]),
    .Q0B(\十二进制计数器或二十四进制的计数器电路_1_q0a [1]), .Q0A(\十二进制计数器或二十四进制的计数器电路_1_q0a [0]),
    .Q1D(\十二进制计数器或二十四进制的计数器电路_1_q0a [7]), .Q1C(\十二进制计数器或二十四进制的计数器电路_1_q0a [6]));  // open: nQCC
  and and_3 (and_3_out, ~Adj1, CPD);  // AND_Gate
  Multiplexer #(.width(4), .enable("false")) multiplexer_4 (
    .in0(multiplexer_3_out), .in1(\十二进制计数器或二十四进制的计数器电路_1_q0a [3:0]), .out(H_l_Alrm), .sel(Set));
  and and_4 (and_4_out, Adj1, CPD);
  Comparator #(.width(4), .mode("unsigned")) comparator_2 (
    .a(\十二进制计数器或二十四进制的计数器电路_1_q0a [7:4]), .b(H_h_R), .eq(comparator_2_eq));  // open: gt, lt
  \六十进制计数器  \u_六十进制计数器_1  (
    .CPU(and_1_out), .CLR(Clr), .CPD(and_4_out), .Adj(1'b1), .Q0D(Min_l_Alarm[3]), .Q0C(Min_l_Alarm[2]),
    .Q0B(Min_l_Alarm[1]), .Q0A(Min_l_Alarm[0]), .Q1D(Min_h_Alarm[3]), .Q1C(Min_h_Alarm[2]),
    .Q1B(Min_h_Alarm[1]), .Q1A(Min_h_Alarm[0]));  // open: nQCC
  Comparator #(.width(4), .mode("unsigned")) comparator_3 (
    .a(\十二进制计数器或二十四进制的计数器电路_1_q0a [3:0]), .b(H_l_R), .eq(comparator_3_eq));  // open: gt, lt
  Comparator #(.width(4), .mode("unsigned")) comparator_4 (
    .a(Min_h_Alarm), .b(Min_h_R), .eq(comparator_4_eq));  // open: gt, lt
  and and_5 (and_5_out, comparator_2_eq, comparator_3_eq, comparator_4_eq, comparator_5_eq);
  Comparator #(.width(4), .mode("unsigned")) comparator_5 (
    .a(Min_l_Alarm), .b(Min_l_R), .eq(comparator_5_eq));  // open: gt, lt
  and and_6 (and_6_out, d_ff_1_q, s_l_R[0]);
  or or_1 (or_1_out, not_2_out, and_7_out);
  and and_7 (and_7_out, ~\四位二进制可逆计数器_1_qd , \四位二进制可逆计数器_1_qc , ~\四位二进制可逆计数器_1_qb , \四位二进制可逆计数器_1_qa );  // AND_Gate
  \四位二进制可逆计数器  \u_四位二进制可逆计数器_1  (
    .CLR(or_1_out), .nLR(1'b1), .A(1'b0), .B(1'b0), .C(1'b0), .D(1'b0), .QA(\四位二进制可逆计数器_1_qa ),
    .QB(\四位二进制可逆计数器_1_qb ), .QC(\四位二进制可逆计数器_1_qc ), .QD(\四位二进制可逆计数器_1_qd ), .CPU(and_6_out), .CPD(1'b0));
  or or_2 (or_2_out, and_7_out, not_2_out);
  D_Flip_Flop d_ff_1 (.clk(and_5_out), .D(d_ff_1_qn), .Q(d_ff_1_q), .Qn(d_ff_1_qn), .preset(1'b0), .reset(or_2_out));
  not not_2 (not_2_out, en);
  and and_8 (out_17, en, d_ff_1_q);
endmodule

module \闹钟测试电路  (
  input  in_1,
  input  in_2,
  input  in_3,
  input  in_4,
  input  [3:0] in_5,
  input  [3:0] in_6,
  input  [3:0] in_7,
  input  [3:0] in_8,
  input  [3:0] in_9,
  input  [3:0] in_10
);

  wire button_1_out, button_2_out, \闹钟_1_out_17 ;
  wire [3:0] \闹钟_1_h_h_alarm , \闹钟_1_h_l_alrm , \闹钟_1_min_h_alarm , \闹钟_1_min_l_alarm ;
  wire [4:0] \闹钟_1_l_0_4 , \闹钟_1_l_5_9 , \闹钟_1_l_10_14 , \闹钟_1_l_15_19 ;

  DotMatrix #(.matrixcols(4), .matrixrows(5)) dotmatrix_1 (
    .col0(\闹钟_1_l_15_19 ), .col1(\闹钟_1_l_10_14 ), .col2(\闹钟_1_l_5_9 ), .col3(\闹钟_1_l_0_4 ));
  Hex_Digit_Display hex_digit_display_1 (.value(\闹钟_1_h_l_alrm ), .dp(1'b0));
  Hex_Digit_Display hex_digit_display_2 (.value(\闹钟_1_h_h_alarm ), .dp(1'b0));
  Hex_Digit_Display hex_digit_display_3 (.value(\闹钟_1_min_h_alarm ), .dp(1'b0));
  Hex_Digit_Display hex_digit_display_4 (.value(\闹钟_1_min_l_alarm ), .dp(1'b0));
  \闹钟  \u_闹钟_1  (
    .H_h_R(in_5), .H_l_R(in_6), .Min_h_R(in_7), .Min_l_R(in_8), .s_h_R(in_9), .s_l_R(in_10), .en(in_4),
    .out_17(\闹钟_1_out_17 ), .L_15_19(\闹钟_1_l_15_19 ), .L_10_14(\闹钟_1_l_10_14 ), .L_5_9(\闹钟_1_l_5_9 ),
    .L_0_4(\闹钟_1_l_0_4 ), .Adj1(in_3), .CPU(button_1_out), .CPD(button_2_out), .Set(in_2), .Clr(in_1),
    .H_h_Alarm(\闹钟_1_h_h_alarm ), .H_l_Alrm(\闹钟_1_h_l_alrm ), .Min_h_Alarm(\闹钟_1_min_h_alarm ),
    .Min_l_Alarm(\闹钟_1_min_l_alarm ));
  Button button_1 (.out(button_1_out));
  LED led_1 (.in(\闹钟_1_out_17 ));
  Button button_2 (.out(button_2_out));
endmodule
