// Logisim project 实验6-CS1906-U201915115-郑舟.circ as structural Verilog: 6 circuits, main circuit sqrX
module sqrX (
  input  [31:0] a,
  input  [31:0] b,
  input  [31:0] c,
  input  [31:0] d,
  output [31:0] a_2_bc_l,
  output [31:0] ab_bd_l,
  output [31:0] ac_cd_l,
  output [31:0] bc_d_2_l
);

  wire [31:0] multiplier_1_out, multiplier_2_out, multiplier_3_out, multiplier_4_out, multiplier_5_out,
       multiplier_6_out, multiplier_7_out;

  Multiplier #(.width(32)) multiplier_1 (.a(a), .b(a), .out(multiplier_1_out), .cin({32{1'b0}}));  // open: cout
  Multiplier #(.width(32)) multiplier_2 (.a(b), .b(c), .out(multiplier_2_out), .cin({32{1'b0}}));  // open: cout
  Multiplier #(.width(32)) multiplier_3 (.a(a), .b(b), .out(multiplier_3_out), .cin({32{1'b0}}));  // open: cout
  Multiplier #(.width(32)) multiplier_4 (.a(b), .b(d), .out(multiplier_4_out), .cin({32{1'b0}}));  // open: cout
  Multiplier #(.width(32)) multiplier_5 (.a(a), .b(c), .out(multiplier_5_out), .cin({32{1'b0}}));  // open: cout
  Multiplier #(.width(32)) multiplier_6 (.a(c), .b(d), .out(multiplier_6_out), .cin({32{1'b0}}));  // open: cout
  Multiplier #(.width(32)) multiplier_7 (.a(d), .b(d), .out(multiplier_7_out), .cin({32{1'b0}}));  // open: cout
  Adder #(.width(32)) adder_1 (.a(multiplier_1_out), .b(multiplier_2_out), .out(a_2_bc_l), .cin(1'b0));  // open: cout
  Adder #(.width(32)) adder_2 (.a(multiplier_3_out), .b(multiplier_4_out), .out(ab_bd_l), .cin(1'b0));  // open: cout
  Adder #(.width(32)) adder_3 (.a(multiplier_5_out), .b(multiplier_6_out), .out(ac_cd_l), .cin(1'b0));  // open: cout
  Adder #(.width(32)) adder_4 (.a(multiplier_2_out), .b(multiplier_7_out), .out(bc_d_2_l), .cin(1'b0));  // open: cout
endmodule

module sqrX_A (
  input  [31:0] a,
  input  [31:0] b,
  input  [31:0] c,
  input  [31:0] d,
  output [31:0] a_prime_prime,
  output [31:0] b_prime_prime,
  output [31:0] c_prime_prime,
  output [31:0] d_prime_prime
);

  wire [31:0] sqrx_1_a_2_bc_l, sqrx_1_ac_cd_l;

  sqrX sqrx_1 (
    .a(a), .b(b), .c(c), .d(d), .a_2_bc_l(sqrx_1_a_2_bc_l), .ab_bd_l(a_prime_prime),
    .ac_cd_l(sqrx_1_ac_cd_l), .bc_d_2_l(c_prime_prime));
  Adder #(.width(32)) adder_1 (.a(sqrx_1_a_2_bc_l), .b(a_prime_prime), .out(b_prime_prime), .cin(1'b0));  // open: cout
  Adder #(.width(32)) adder_2 (.a(sqrx_1_ac_cd_l), .b(c_prime_prime), .out(d_prime_prime), .cin(1'b0));  // open: cout
endmodule

module Fibo (
  input  start,
  input  clr,
  input  clk,
  input  ni_1,
  output [31:0] Fi
);

  wire [31:0] multiplexer_1_out, multiplexer_2_out, multiplexer_3_out, multiplexer_4_out, multiplexer_6_out,
       multiplexer_7_out, multiplexer_8_out, multiplexer_9_out, register_1_q, register_2_q, register_3_q,
       register_4_q, sqrx_1_a_2_bc_l, sqrx_1_ab_bd_l, sqrx_1_ac_cd_l, sqrx_1_bc_d_2_l,
       sqrx_a_1_a_prime_prime, sqrx_a_1_b_prime_prime, sqrx_a_1_c_prime_prime, sqrx_a_1_d_prime_prime;

  Multiplexer #(.width(32), .enable("false")) multiplexer_1 (
    .in0({32{1'b0}}), .in1(multiplexer_6_out), .out(multiplexer_1_out), .sel(start));
  Multiplexer #(.width(32), .enable("false")) multiplexer_2 (
    .in0(32'h1), .in1(multiplexer_7_out), .out(multiplexer_2_out), .sel(start));
  Multiplexer #(.width(32), .enable("false")) multiplexer_3 (
    .in0(32'h1), .in1(multiplexer_8_out), .out(multiplexer_3_out), .sel(start));
  Multiplexer #(.width(32), .enable("false")) multiplexer_4 (
    .in0(32'h1), .in1(multiplexer_9_out), .out(multiplexer_4_out), .sel(start));
  Register #(.width(32), .Select("low")) register_1 (
    .D(multiplexer_1_out), .en(1'b1), .Q(register_1_q), .clk(clk), .clr(clr), .cs(1'b0), .preset(1'b0));
  Register #(.width(32), .Select("low")) register_2 (
    .D(multiplexer_2_out), .en(1'b1), .Q(register_2_q), .clk(clk), .clr(clr), .cs(1'b0), .preset(1'b0));
  Register #(.width(32), .Select("low")) register_3 (
    .D(multiplexer_3_out), .en(1'b1), .Q(register_3_q), .clk(clk), .clr(clr), .cs(1'b0), .preset(1'b0));
  Register #(.width(32), .Select("low")) register_4 (
    .D(multiplexer_4_out), .en(1'b1), .Q(register_4_q), .clk(clk), .clr(clr), .cs(1'b0), .preset(1'b0));
  sqrX sqrx_1 (
    .a(register_1_q), .b(register_2_q), .c(register_3_q), .d(register_4_q), .a_2_bc_l(sqrx_1_a_2_bc_l),
    .ab_bd_l(sqrx_1_ab_bd_l), .ac_cd_l(sqrx_1_ac_cd_l), .bc_d_2_l(sqrx_1_bc_d_2_l));
  sqrX_A sqrx_a_1 (
    .a(register_1_q), .b(register_2_q), .c(register_3_q), .d(register_4_q),
    .a_prime_prime(sqrx_a_1_a_prime_prime), .b_prime_prime(sqrx_a_1_b_prime_prime),
    .c_prime_prime(sqrx_a_1_c_prime_prime), .d_prime_prime(sqrx_a_1_d_prime_prime));
  Multiplexer #(.width(32), .enable("false")) multiplexer_5 (
    .in0({32{1'b0}}), .in1(register_2_q), .out(Fi), .sel(start));
  Multiplexer #(.width(32), .enable("false")) multiplexer_6 (
    .in0(sqrx_1_a_2_bc_l), .in1(sqrx_a_1_a_prime_prime), .out(multiplexer_6_out), .sel(ni_1));
  Multiplexer #(.width(32), .enable("false")) multiplexer_7 (
    .in0(sqrx_1_ab_bd_l), .in1(sqrx_a_1_b_prime_prime), .out(multiplexer_7_out), .sel(ni_1));
  Multiplexer #(.width(32), .enable("false")) multiplexer_8 (
    .in0(sqrx_1_ac_cd_l), .in1(sqrx_a_1_c_prime_prime), .out(multiplexer_8_out), .sel(ni_1));
  Multiplexer #(.width(32), .enable("false")) multiplexer_9 (
    .in0(sqrx_1_bc_d_2_l), .in1(sqrx_a_1_d_prime_prime), .out(multiplexer_9_out), .sel(ni_1));
endmodule

module \Fibonacci数显示模块  (
  input  [31:0] in_1,
  output [3:0] D9,
  output [3:0] D8,
  output [3:0] D7,
  output [3:0] D6,
  output [3:0] D5,
  output [3:0] D4,
  output [3:0] D3,
  output [3:0] D2,
  output [3:0] D1,
  output [3:0] D0
);

  wire [31:0] divider_1_rem, divider_2_rem, divider_3_rem, divider_4_rem, divider_5_rem, divider_6_rem,
       divider_7_rem, divider_8_rem;
  wire [31:4] divider_1_out, divider_2_out, divider_3_out, divider_4_out, divider_5_out, divider_6_out,
       divider_7_out, divider_8_out, divider_9_out, divider_9_rem;

  Divider #(.width(32)) divider_1 (
    .a(in_1), .b(32'h3b9aca00), .out({divider_1_out, D9}), .rem(divider_1_rem));  // open: upper
  Divider #(.width(32)) divider_2 (
    .a(divider_1_rem), .b(32'h5f5e100), .out({divider_2_out, D8}), .rem(divider_2_rem));  // open: upper
  Divider #(.width(32)) divider_3 (
    .a(divider_2_rem), .b(32'h989680), .out({divider_3_out, D7}), .rem(divider_3_rem));  // open: upper
  Divider #(.width(32)) divider_4 (
    .a(divider_3_rem), .b(32'hf4240), .out({divider_4_out, D6}), .rem(divider_4_rem));  // open: upper
  Divider #(.width(32)) divider_5 (
    .a(divider_4_rem), .b(32'h186a0), .out({divider_5_out, D5}), .rem(divider_5_rem));  // open: upper
  Divider #(.width(32)) divider_6 (
    .a(divider_5_rem), .b(32'h2710), .out({divider_6_out, D4}), .rem(divider_6_rem));  // open: upper
  Divider #(.width(32)) divider_7 (
    .a(divider_6_rem), .b(32'h3e8), .out({divider_7_out, D3}), .rem(divider_7_rem));  // open: upper
  Divider #(.width(32)) divider_8 (
    .a(divider_7_rem), .b(32'h64), .out({divider_8_out, D2}), .rem(divider_8_rem));  // open: upper
  Divider #(.width(32)) divider_9 (
    .a(divider_8_rem), .b(32'ha), .out({divider_9_out, D1}), .rem({divider_9_rem, D0}));  // open: upper
endmodule

module \斐波那契数列_Fibonacci_数列计算器  (
  input  [5:0] n,
  input  clear,
  input  clock,
  output [3:0] D9,
  output [3:0] D8,
  output [3:0] D7,
  output [3:0] D6,
  output [3:0] D5,
  output [3:0] D4,
  output [3:0] D3,
  output [3:0] D2,
  output [3:0] D1,
  output [3:0] D0
);

  wire and_1_out, comparator_1_lt, d_ff_1_q, or_1_out, or_2_out, shift_register_1_out;
  wire [7:0] counter_1_q;
  wire [31:0] fibo_1_fi;

  or or_1 (or_1_out, clear, and_1_out);
  Shift_Register #(.length(6)) shift_register_1 (
    .shift(1'b1), .in(1'b0), .clk(or_1_out), .out(shift_register_1_out), .load(clear), .clr(1'b0), .d0(n[0]),
    .d1(n[1]), .d2(n[2]), .d3(n[3]), .d4(n[4]), .d5(n[5]));  // open: q0, q1, q2, q3, q4, q5
  Counter #(.ongoal("stay")) counter_1 (
    .load(1'b0), .count(1'b1), .Q(counter_1_q), .clk(clock), .clr(clear), .preset(1'b0), .down(1'b0));  // open: D, carry
  or or_2 (or_2_out, d_ff_1_q, shift_register_1_out);
  Comparator #(.mode("unsigned")) comparator_1 (.a(counter_1_q), .b(8'h6), .lt(comparator_1_lt));  // open: gt, eq
  D_Flip_Flop d_ff_1 (.clk(clock), .D(or_2_out), .Q(d_ff_1_q), .preset(1'b0), .reset(clear));  // open: Qn
  and and_1 (and_1_out, comparator_1_lt, clock);
  Fibo fibo_1 (.start(d_ff_1_q), .clr(clear), .clk(and_1_out), .ni_1(shift_register_1_out), .Fi(fibo_1_fi));
  \Fibonacci数显示模块  \fibonacci数显示模块_1  (
    .in_1(fibo_1_fi), .D9(D9), .D8(D8), .D7(D7), .D6(D6), .D5(D5), .D4(D4), .D3(D3), .D2(D2), .D1(D1), .D0(D0));
endmodule

module \斐波那契数列_Fibonacci_数列计算器测试电路  (
  input  [5:0] in_1
);

  wire button_1_out, button_2_out;
  wire [3:0] \斐波那契数列_fibonacci_数列计算器_1_d0 , \斐波那契数列_fibonacci_数列计算器_1_d1 , \斐波那契数列_fibonacci_数列计算器_1_d2 ,
       \斐波那契数列_fibonacci_数列计算器_1_d3 , \斐波那契数列_fibonacci_数列计算器_1_d4 , \斐波那契数列_fibonacci_数列计算器_1_d5 ,
       \斐波那契数列_fibonacci_数列计算器_1_d6 , \斐波那契数列_fibonacci_数列计算器_1_d7 , \斐波那契数列_fibonacci_数列计算器_1_d8 ,
       \斐波那契数列_fibonacci_数列计算器_1_d9 ;

  Button button_1 (.out(button_1_out));
  Button button_2 (.out(button_2_out));
  Hex_Digit_Display hex_digit_display_1 (.value(\斐波那契数列_fibonacci_数列计算器_1_d9 ), .dp(1'b0));
  \斐波那契数列_Fibonacci_数列计算器  \u_斐波那契数列_fibonacci_数列计算器_1  (
    .n(in_1), .clear(button_1_out), .clock(button_2_out), .D9(\斐波那契数列_fibonacci_数列计算器_1_d9 ),
    .D8(\斐波那契数列_fibonacci_数列计算器_1_d8 ), .D7(\斐波那契数列_fibonacci_数列计算器_1_d7 ),
    .D6(\斐波那契数列_fibonacci_数列计算器_1_d6 ), .D5(\斐波那契数列_fibonacci_数列计算器_1_d5 ),
    .D4(\斐波那契数列_fibonacci_数列计算器_1_d4 ), .D3(\斐波那契数列_fibonacci_数列计算器_1_d3 ),
    .D2(\斐波那契数列_fibonacci_数列计算器_1_d2 ), .D1(\斐波那契数列_fibonacci_数列计算器_1_d1 ), .D0(\斐波那契数列_fibonacci_数列计算器_1_d0 ));
  Hex_Digit_Display hex_digit_display_2 (.value(\斐波那契数列_fibonacci_数列计算器_1_d8 ), .dp(1'b0));
  Hex_Digit_Display hex_digit_display_3 (.value(\斐波那契数列_fibonacci_数列计算器_1_d7 ), .dp(1'b0));
  Hex_Digit_Display hex_digit_display_4 (.value(\斐波那契数列_fibonacci_数列计算器_1_d6 ), .dp(1'b0));
  Hex_Digit_Display hex_digit_display_5 (.value(\斐波那契数列_fibonacci_数列计算器_1_d5 ), .dp(1'b0));
  Hex_Digit_Display hex_digit_display_6 (.value(\斐波那契数列_fibonacci_数列计算器_1_d3 ), .dp(1'b0));
  Hex_Digit_Display hex_digit_display_7 (.value(\斐波那契数列_fibonacci_数列计算器_1_d4 ), .dp(1'b0));
  Hex_Digit_Display hex_digit_display_8 (.value(\斐波那契数列_fibonacci_数列计算器_1_d1 ), .dp(1'b0));
  Hex_Digit_Display hex_digit_display_9 (.value(\斐波那契数列_fibonacci_数列计算器_1_d2 ), .dp(1'b0));
  Hex_Digit_Display hex_digit_display_10 (.value(\斐波那契数列_fibonacci_数列计算器_1_d0 ), .dp(1'b0));
endmodule
